// Logisim project Matic_Bernot_Logisim_Digitalna_ura.circ as structural Verilog: 2 circuits, main circuit Binarna_ura
module binary_clock (
  input  reset,
  input  [3:0] sel,
  input  [3:0] data_time,
  input  clk,
  output [3:0] h10,
  output [3:0] h1,
  output [3:0] m10,
  output [3:0] m1,
  output [3:0] s10,
  output [3:0] s1
);

  wire and_1_out, and_2_out, and_3_out, and_4_out, and_5_out, comparator_1_eq, counter_1_carry,
       counter_2_carry, counter_3_carry, counter_4_carry, counter_5_carry, counter_6_carry, R, weh1, weh10,
       wem1, wem10, wes1, wes10;
  wire [3:0] register_1_q, register_2_q, register_3_q, register_4_q, register_5_q, register_6_q;

  Decoder #(.select(4)) decoder_1 (
    .out1(weh10), .out2(weh1), .out4(wem10), .out5(wem1), .out7(wes10), .out8(wes1), .sel(sel));  // open: out0, out3, out6, out9, out10, out11, out12, out13, out14, out15, en
  // Probe on data_time
  Register #(.width(4)) register_1 (.D(data_time), .en(1'b1), .clk(clk), .Q(register_1_q), .clr(R));
  // Probe on data_time
  Register #(.width(4)) register_2 (.D(data_time), .en(1'b1), .clk(clk), .Q(register_2_q), .clr(R));
  // Probe on data_time
  Register #(.width(4)) register_3 (.D(data_time), .en(1'b1), .clk(clk), .Q(register_3_q), .clr(R));
  // Probe on data_time
  Register #(.width(4)) register_4 (.D(data_time), .en(1'b1), .clk(clk), .Q(register_4_q), .clr(R));
  // Probe on data_time
  Register #(.width(4)) register_5 (.D(data_time), .en(1'b1), .clk(clk), .Q(register_5_q), .clr(R));
  // Probe on data_time
  Register #(.width(4)) register_6 (.D(data_time), .en(1'b1), .clk(clk), .Q(register_6_q), .clr(R));
  or or_1 (R, and_1_out, reset);
  Counter #(.max('h2), .width(4)) counter_1 (
    .clr(R), .load(weh10), .count(and_3_out), .clk(clk), .D(register_1_q), .carry(counter_1_carry), .Q(h10));  // open: up
  Counter #(.max('h9), .width(4)) counter_2 (
    .clr(R), .load(weh1), .count(and_4_out), .clk(clk), .D(register_2_q), .carry(counter_2_carry), .Q(h1));  // open: up
  Counter #(.max('h5), .width(4)) counter_3 (
    .clr(R), .load(wem10), .count(and_5_out), .clk(clk), .D(register_3_q), .carry(counter_3_carry), .Q(m10));  // open: up
  Counter #(.max('h9), .width(4)) counter_4 (
    .clr(R), .load(wem1), .count(and_2_out), .clk(clk), .D(register_4_q), .carry(counter_4_carry), .Q(m1));  // open: up
  Counter #(.max('h5), .width(4)) counter_5 (
    .clr(R), .load(wes10), .count(counter_6_carry), .clk(clk), .D(register_5_q), .carry(counter_5_carry),
    .Q(s10));  // open: up
  Counter #(.max('h9), .width(4)) counter_6 (
    .clr(R), .load(wes1), .count(1'b1), .clk(clk), .D(register_6_q), .carry(counter_6_carry), .Q(s1));  // open: up
  // Probe on 4'b0100
  and and_1 (and_1_out, comparator_1_eq, counter_1_carry);
  Comparator #(.width(4)) comparator_1 (.a(4'b0100), .b(h1), .eq(comparator_1_eq));  // open: gt, lt
  and and_2 (and_2_out, counter_5_carry, counter_6_carry);
  and and_3 (and_3_out, counter_2_carry, and_4_out);
  and and_4 (and_4_out, counter_3_carry, and_5_out);
  and and_5 (and_5_out, counter_4_carry, and_2_out);
  Hex_Digit_Display #(.decimalPoint("false")) hex_digit_display_1 (.value(h10));
  Hex_Digit_Display #(.decimalPoint("false")) hex_digit_display_2 (.value(h1));
  Hex_Digit_Display #(.decimalPoint("false")) hex_digit_display_3 (.value(m10));
  Hex_Digit_Display #(.decimalPoint("false")) hex_digit_display_4 (.value(m1));
  Hex_Digit_Display #(.decimalPoint("false")) hex_digit_display_5 (.value(s10));
  Hex_Digit_Display #(.decimalPoint("false")) hex_digit_display_6 (.value(s1));
endmodule

module Binarna_ura (
  input  in_1
);

  wire CLKIN, controlled_buffer_1_out, keyboard_1_avail, or_1_out, Press_9x_out, Res_bin;
  wire [3:0] bitselector_1_out, counter_1_q, h1, h10, m1, m10, s1, s10;
  wire [6:0] keyboard_1_data;

  Button Press_9x (.out(Press_9x_out));
  Button Reset_bin_clk (.out(Res_bin));
  Clock clock_1 (.out(CLKIN));
  Keyboard keyboard_1 (.clk(Press_9x_out), .re(1'b1), .clr(Res_bin), .avail(keyboard_1_avail), .data(keyboard_1_data));
  assign controlled_buffer_1_out = keyboard_1_avail ? Press_9x_out : 1'bz;  // Controlled_Buffer controlled_buffer_1
  Counter #(.max('h8), .width(4)) counter_1 (
    .count(1'b1), .Q(counter_1_q), .clk(Press_9x_out), .clr(Res_bin));  // open: load, D, carry, up
  // Probe on keyboard_1_data
  BitSelector #(.group(4), .width(7)) bitselector_1 (.in(keyboard_1_data), .out(bitselector_1_out), .sel(in_1));
  or or_1 (or_1_out, CLKIN, Press_9x_out);
  binary_clock binary_clock_1 (
    .reset(Res_bin), .sel(counter_1_q), .data_time(bitselector_1_out), .clk(or_1_out), .h10(h10), .h1(h1),
    .m10(m10), .m1(m1), .s10(s10), .s1(s1));
  // RGBLED rgbled_1: pin names not known; wires that end beside it: h10[1]
  // RGBLED rgbled_2: pin names not known; wires that end beside it: h10[0]
  Hex_Digit_Display #(.decimalPoint("false")) hex_digit_display_1 (.value(h10));
  Hex_Digit_Display #(.decimalPoint("false")) hex_digit_display_2 (.value(h1));
  // RGBLED rgbled_3: pin names not known; wires that end beside it: h1[3]
  // RGBLED rgbled_4: pin names not known; wires that end beside it: h1[2]
  // RGBLED rgbled_5: pin names not known; wires that end beside it: h1[1]
  // RGBLED rgbled_6: pin names not known; wires that end beside it: h1[0]
  Hex_Digit_Display #(.decimalPoint("false")) hex_digit_display_3 (.value(m10));
  Hex_Digit_Display #(.decimalPoint("false")) hex_digit_display_4 (.value(m1));
  // RGBLED rgbled_7: pin names not known; wires that end beside it: m1[3]
  // RGBLED rgbled_8: pin names not known; wires that end beside it: m10[2]
  // RGBLED rgbled_9: pin names not known; wires that end beside it: m1[2]
  // RGBLED rgbled_10: pin names not known; wires that end beside it: m10[1]
  // RGBLED rgbled_11: pin names not known; wires that end beside it: m1[1]
  // RGBLED rgbled_12: pin names not known; wires that end beside it: m10[0]
  // RGBLED rgbled_13: pin names not known; wires that end beside it: m1[0]
  Hex_Digit_Display #(.decimalPoint("false")) hex_digit_display_5 (.value(s10));
  // RGBLED rgbled_14: pin names not known; wires that end beside it: s10[2]
  // RGBLED rgbled_15: pin names not known; wires that end beside it: s10[1]
  // RGBLED rgbled_16: pin names not known; wires that end beside it: s10[0]
  Hex_Digit_Display #(.decimalPoint("false")) hex_digit_display_6 (.value(s1));
  // RGBLED rgbled_17: pin names not known; wires that end beside it: s1[3]
  // RGBLED rgbled_18: pin names not known; wires that end beside it: s1[2]
  // RGBLED rgbled_19: pin names not known; wires that end beside it: s1[1]
  // RGBLED rgbled_20: pin names not known; wires that end beside it: s1[0]

  // Notes on the sheet:
  //   Keyboard (enter time)
  //   Binary Clock
  //   2. Press a button 9 times
  //   1. Enter time in format hh:mm:ss
  //   example: 12:34:56
  //   3. Auto tick at 2.0 Hz (for seconds)
  //   •
  //   •
  //   •
  //   •
endmodule
