// Logisim project Thuma_MiMo_FPU.circ as structural Verilog: 2 circuits, main circuit main
module main (
);

  wire CLK, fpu_1_nanerror, fpu_1_zero, fpuenable, fswrite, reset;
  wire [3:0] fsselADDR;
  wire [15:0] data, fhreg, fpu_1_h0, fpu_1_h1, fpu_1_h2, fpu_1_h3, fpu_1_h4, fpu_1_h5, fpu_1_h6, fpu_1_h7,
       fpu_1_h8, fpu_1_h9, fpu_1_h10, fpu_1_h11, fpu_1_h12, fpu_1_h13, fpu_1_h14, fpu_1_h15, fpu_1_results0,
       fpu_1_results1;
  wire [31:0] fpu_1_s0, fpu_1_s1, fpu_1_s2, fpu_1_s3, fpu_1_s4, fpu_1_s5, fpu_1_s6, fpu_1_s7;

  // Probe on fpu_1_h0
  // Probe on fpu_1_h0
  FPU fpu_1 (
    .data(data), .Reset(reset), .clock(CLK), .fpuenable(fpuenable), .fswrite(fswrite), .fsselADDR(fsselADDR),
    .h0(fpu_1_h0), .h1(fpu_1_h1), .h2(fpu_1_h2), .h3(fpu_1_h3), .NaNerror(fpu_1_nanerror), .h4(fpu_1_h4),
    .h5(fpu_1_h5), .h6(fpu_1_h6), .h7(fpu_1_h7), .h8(fpu_1_h8), .h9(fpu_1_h9), .h10(fpu_1_h10),
    .h11(fpu_1_h11), .Zero(fpu_1_zero), .h12(fpu_1_h12), .h13(fpu_1_h13), .h14(fpu_1_h14), .h15(fpu_1_h15),
    .fsreg(fhreg), .s0(fpu_1_s0), .s1(fpu_1_s1), .s2(fpu_1_s2), .s3(fpu_1_s3), .s4(fpu_1_s4), .s5(fpu_1_s5),
    .s6(fpu_1_s6), .s7(fpu_1_s7), .resultS0(fpu_1_results0), .resultS1(fpu_1_results1));
  // Probe on fpu_1_h1
  // Probe on fpu_1_h1
  // Probe on fpu_1_h2
  // Probe on fpu_1_h2
  // Probe on fpu_1_h3
  // Probe on fpu_1_h3
  LED led_1 (.in(fpu_1_nanerror));
  LED led_2 (.in(fpu_1_nanerror));
  // Probe on fpu_1_h4
  // Probe on fpu_1_h4
  // Probe on fpu_1_h5
  // Probe on fpu_1_h5
  // Probe on fpu_1_h6
  // Probe on fpu_1_h6
  // Probe on fpu_1_h7
  // Probe on fpu_1_h7
  // Probe on fpu_1_h8
  // Probe on fpu_1_h8
  // Probe on fpu_1_h9
  // Probe on fpu_1_h9
  // Probe on fpu_1_h10
  // Probe on fpu_1_h10
  // Probe on fpu_1_h11
  // Probe on fpu_1_h11
  LED led_3 (.in(fpu_1_zero));
  LED led_4 (.in(fpu_1_zero));
  // Probe on fpu_1_h12
  // Probe on fpu_1_h12
  // Probe on fpu_1_h13
  // Probe on fpu_1_h13
  // Probe on fpu_1_h14
  // Probe on fpu_1_h14
  // Probe on fpu_1_h15
  // Probe on fpu_1_h15
  // Probe on fpu_1_s0
  // Probe on fpu_1_s0
  // Probe on fpu_1_s1
  // Probe on fpu_1_s1
  // Probe on fpu_1_s2
  // Probe on fpu_1_s2
  // Probe on fpu_1_s3
  // Probe on fpu_1_s3
  // Probe on fpu_1_s4
  // Probe on fpu_1_s4
  // Probe on fpu_1_s5
  // Probe on fpu_1_s5
  // Probe on fpu_1_s6
  // Probe on fpu_1_s6
  // Probe on fpu_1_s7
  // Probe on fpu_1_s7
  // Probe on {fpu_1_results1, fpu_1_results0}
  // Probe on {fpu_1_results1, fpu_1_results0}
  // Probe on fhreg
  // Probe on fhreg
endmodule

module FPU (
  input  [15:0] data,
  input  Reset,
  input  clock,
  input  fpuenable,
  input  fswrite,
  input  [3:0] fsselADDR,
  output [15:0] h0,
  output [15:0] h1,
  output [15:0] h2,
  output [15:0] h3,
  output NaNerror,
  output [15:0] h4,
  output [15:0] h5,
  output [15:0] h6,
  output [15:0] h7,
  output [15:0] h8,
  output [15:0] h9,
  output [15:0] h10,
  output [15:0] h11,
  output Zero,
  output [15:0] h12,
  output [15:0] h13,
  output [15:0] h14,
  output [15:0] h15,
  output [15:0] fsreg,
  output [31:0] s0,
  output [31:0] s1,
  output [31:0] s2,
  output [31:0] s3,
  output [31:0] s4,
  output [31:0] s5,
  output [31:0] s6,
  output [31:0] s7,
  output [15:0] resultS0,
  output [15:0] resultS1
);

  wire and_2_out, and_3_out, and_4_out, demultiplexer_1_out0, demultiplexer_1_out1, demultiplexer_1_out2,
       demultiplexer_1_out3, demultiplexer_1_out4, demultiplexer_1_out5, demultiplexer_1_out6,
       demultiplexer_1_out7, demultiplexer_1_out8, demultiplexer_1_out9, demultiplexer_1_out10,
       demultiplexer_1_out11, demultiplexer_1_out12, demultiplexer_1_out13, demultiplexer_1_out14,
       demultiplexer_1_out15, not_1_out, not_2_out, or_1_out, or_2_out, or_3_out, resultwrite, undriven,
       undriven_2, undriven_3, undriven_4, undriven_5, undriven_6;
  wire [3:0] multiplexer_1_out, multiplexer_3_out;
  wire [15:0] fdreg, fpadder_2_out, fpadder_4_out, fpdivider_2_out, fpmultiplier_5_out, fpmultiplier_6_out,
       fpsubtractor_2_out, ftreg, multiplexer_2_out, result;
  wire [31:0] fdregD, fpadder_1_out, fpadder_3_out, fpdivider_1_out, fpmultiplier_1_out, fpmultiplier_2_out,
       fpmultiplier_3_out, fpmultiplier_4_out, fpmultiplier_7_out, fpmultiplier_8_out, fpsubtractor_1_out,
       fpsubtractor_3_out, fsregS, ftregS, multiplexer_11_out, shifter_1_out, y;

  not not_1 (not_1_out, data[15]);
  Multiplexer #(.width(4)) multiplexer_1 (
    .in0(fsselADDR), .in1(data[11:8]), .out(multiplexer_1_out), .sel(resultwrite));
  and and_1 (resultwrite, fpuenable, not_1_out);
  Multiplexer #(.width(16)) multiplexer_2 (.in0(data), .in1(result), .out(multiplexer_2_out), .sel(resultwrite));
  Demultiplexer #(.select(4)) demultiplexer_1 (
    .out0(demultiplexer_1_out0), .out1(demultiplexer_1_out1), .out2(demultiplexer_1_out2),
    .out3(demultiplexer_1_out3), .out4(demultiplexer_1_out4), .out5(demultiplexer_1_out5),
    .out6(demultiplexer_1_out6), .out7(demultiplexer_1_out7), .out8(demultiplexer_1_out8),
    .out9(demultiplexer_1_out9), .out10(demultiplexer_1_out10), .out11(demultiplexer_1_out11),
    .out12(demultiplexer_1_out12), .out13(demultiplexer_1_out13), .out14(demultiplexer_1_out14),
    .out15(demultiplexer_1_out15), .in(or_1_out), .sel(multiplexer_1_out));
  or or_1 (or_1_out, fswrite, resultwrite);
  Register #(.width(16)) register_1 (
    .D(multiplexer_2_out), .en(demultiplexer_1_out0), .Q(h0), .clk(clock), .clr(Reset));
  Register #(.width(16)) register_2 (
    .D(multiplexer_2_out), .en(demultiplexer_1_out1), .Q(h1), .clk(clock), .clr(Reset));
  Register #(.width(16)) register_3 (
    .D(multiplexer_2_out), .en(demultiplexer_1_out2), .Q(h2), .clk(clock), .clr(Reset));
  Register #(.width(16)) register_4 (
    .D(multiplexer_2_out), .en(demultiplexer_1_out3), .Q(h3), .clk(clock), .clr(Reset));
  Register #(.width(16)) register_5 (
    .D(multiplexer_2_out), .en(demultiplexer_1_out4), .Q(h4), .clk(clock), .clr(Reset));
  Register #(.width(16)) register_6 (
    .D(multiplexer_2_out), .en(demultiplexer_1_out5), .Q(h5), .clk(clock), .clr(Reset));
  Register #(.width(16)) register_7 (
    .D(multiplexer_2_out), .en(demultiplexer_1_out6), .Q(h6), .clk(clock), .clr(Reset));
  Register #(.width(16)) register_8 (
    .D(multiplexer_2_out), .en(demultiplexer_1_out7), .Q(h7), .clk(clock), .clr(Reset));
  Register #(.width(16)) register_9 (
    .D(multiplexer_2_out), .en(demultiplexer_1_out8), .Q(h8), .clk(clock), .clr(Reset));
  Register #(.width(16)) register_10 (
    .D(multiplexer_2_out), .en(demultiplexer_1_out9), .Q(h9), .clk(clock), .clr(Reset));
  Register #(.width(16)) register_11 (
    .D(multiplexer_2_out), .en(demultiplexer_1_out10), .Q(h10), .clk(clock), .clr(Reset));
  Register #(.width(16)) register_12 (
    .D(multiplexer_2_out), .en(demultiplexer_1_out11), .Q(h11), .clk(clock), .clr(Reset));
  Register #(.width(16)) register_13 (
    .D(multiplexer_2_out), .en(demultiplexer_1_out12), .Q(h12), .clk(clock), .clr(Reset));
  Register #(.width(16)) register_14 (
    .D(multiplexer_2_out), .en(demultiplexer_1_out13), .Q(h13), .clk(clock), .clr(Reset));
  Register #(.width(16)) register_15 (
    .D(multiplexer_2_out), .en(demultiplexer_1_out14), .Q(h14), .clk(clock), .clr(Reset));
  Register #(.width(16)) register_16 (
    .D(multiplexer_2_out), .en(demultiplexer_1_out15), .Q(h15), .clk(clock), .clr(Reset));
  Multiplexer #(.width(4)) multiplexer_3 (.in0(fsselADDR), .in1(data[7:4]), .out(multiplexer_3_out), .sel(fpuenable));
  Multiplexer #(.select(4), .width(16)) multiplexer_4 (
    .in0(h0), .in1(h1), .in2(h2), .in3(h3), .in4(h4), .in5(h5), .in6(h6), .in7(h7), .in8(h8), .in9(h9),
    .in10(h10), .in11(h11), .in12(h12), .in13(h13), .in14(resultS0), .in15(resultS1), .out(fsreg),
    .sel(multiplexer_3_out));
  Multiplexer #(.select(4), .width(16)) multiplexer_5 (
    .in0(h0), .in1(h1), .in2(h2), .in3(h3), .in4(h4), .in5(h5), .in6(h6), .in7(h7), .in8(h8), .in9(h9),
    .in10(h10), .in11(h11), .in12(h12), .in13(h13), .in14(h14), .in15(h15), .out(ftreg), .sel(data[3:0]));
  Multiplexer #(.select(4), .width(16)) multiplexer_6 (
    .in0(h0), .in1(h1), .in2(h2), .in3(h3), .in4(h4), .in5(h5), .in6(h6), .in7(h7), .in8(h8), .in9(h9),
    .in10(h10), .in11(h11), .in12(h12), .in13(h13), .in14(h14), .in15(h15), .out(fdreg), .sel(data[11:8]));
  Multiplexer #(.enable("true"), .select(4), .width(32)) multiplexer_7 (
    .in0({h1, h0}), .in1({h3, h2}), .in2({h5, h4}), .in3({h7, h6}), .in4({h9, h8}), .in5({h11, h10}),
    .in6({h13, h12}), .in7({h15, h14}), .out(fsregS), .sel(data[7:4]), .en(data[15]));  // open: in8, in9, in10, in11, in12, in13, in14, in15
  Multiplexer #(.enable("true"), .select(4), .width(32)) multiplexer_8 (
    .in0({h1, h0}), .in1({h3, h2}), .in2({h5, h4}), .in3({h7, h6}), .in4({h9, h8}), .in5({h11, h10}),
    .in6({h13, h12}), .in7({h15, h14}), .out(ftregS), .sel(data[3:0]), .en(data[15]));  // open: in8, in9, in10, in11, in12, in13, in14, in15
  FPMultiplier fpmultiplier_1 (.a(fsregS), .b(32'h3f000000), .out(fpmultiplier_1_out));
  FPAdder fpadder_1 (.a(fsregS), .b(ftregS), .out(fpadder_1_out));
  FPSubtractor fpsubtractor_1 (.a(fsregS), .b(ftregS), .out(fpsubtractor_1_out));
  FPMultiplier fpmultiplier_2 (.a(fsregS), .b(ftregS), .out(fpmultiplier_2_out));
  FPDivider fpdivider_1 (.a(fsregS), .b(ftregS), .out(fpdivider_1_out));
  FPMultiplier fpmultiplier_3 (.a(fsregS), .b(ftregS), .out(fpmultiplier_3_out));
  Shifter #(.shift("lr"), .width(32)) shifter_1 (.in(fsregS), .\dist (5'b00001), .out(shifter_1_out));
  FPMultiplier fpmultiplier_4 (.a(fpmultiplier_1_out), .b(y), .out(fpmultiplier_4_out));
  FPAdder #(.fpwidth(16)) fpadder_2 (.a(fsreg), .b(ftreg), .out(fpadder_2_out));
  FPSubtractor #(.fpwidth(16)) fpsubtractor_2 (.a(fsreg), .b(ftreg), .out(fpsubtractor_2_out));
  FPMultiplier #(.fpwidth(16)) fpmultiplier_5 (.a(fsreg), .b(ftreg), .out(fpmultiplier_5_out));
  FPDivider #(.fpwidth(16)) fpdivider_2 (.a(fsreg), .b(ftreg), .out(fpdivider_2_out));
  FPMultiplier #(.fpwidth(16)) fpmultiplier_6 (.a(fsreg), .b(ftreg), .out(fpmultiplier_6_out));
  // Probe on data[14:12]
  FPAdder fpadder_3 (.a(fpmultiplier_3_out), .b(fdregD), .out(fpadder_3_out));
  Subtractor #(.width(32)) subtractor_1 (.a(32'h5f3759df), .b(shifter_1_out), .out(y));  // open: bin, bout
  FPMultiplier fpmultiplier_7 (.a(fpmultiplier_4_out), .b(y), .out(fpmultiplier_7_out));
  FPAdder #(.fpwidth(16)) fpadder_4 (.a(fpmultiplier_6_out), .b(fdreg), .out(fpadder_4_out));
  and and_2 (and_2_out, not_2_out, fpuenable);
  not not_2 (not_2_out, data[15]);
  Multiplexer #(.enable("true"), .select(3), .width(16)) multiplexer_9 (
    .in0(fpadder_2_out), .in1(fpsubtractor_2_out), .in2(fpmultiplier_5_out), .in3(fpdivider_2_out),
    .in4(fpadder_4_out), .out(result), .sel(data[14:12]), .en(and_2_out));  // open: in5, in6, in7
  FPSubtractor fpsubtractor_3 (.a(32'h3fc00000), .b(fpmultiplier_7_out), .out(fpsubtractor_3_out));
  FPMultiplier fpmultiplier_8 (.a(fpsubtractor_3_out), .b(y), .out(fpmultiplier_8_out));
  or or_2 (or_2_out, undriven_5, undriven_6);
  or or_3 (or_3_out, result[0], result[1], result[2], result[3], result[4], result[5], result[6], result[7], result[9], result[10], result[11], result[12], result[13], result[14], result[15], result[8]);
  // Probe on data[14:12]
  and and_3 (and_3_out, data[15], fpuenable);
  Multiplexer #(.select(3)) multiplexer_10 (
    .in0(undriven), .in1(undriven_2), .in2(undriven_3), .in3(undriven_4), .in4(or_2_out), .out(NaNerror),
    .sel(data[14:12]));  // open: in5, in6, in7
  not not_3 (Zero, or_3_out);
  Multiplexer #(.enable("true"), .select(3), .width(32)) multiplexer_11 (
    .in0(fpadder_1_out), .in1(fpsubtractor_1_out), .in2(fpmultiplier_2_out), .in3(fpdivider_1_out),
    .in4(fpadder_3_out), .in5(fpmultiplier_8_out), .out(multiplexer_11_out), .sel(data[14:12]), .en(and_3_out));  // open: in6, in7
  and and_4 (and_4_out, fpuenable, data[15]);
  Register #(.width(16)) register_17 (
    .D(multiplexer_11_out[15:0]), .en(and_4_out), .Q(resultS0), .clk(clock), .clr(Reset));
  Register #(.width(16)) register_18 (
    .D(multiplexer_11_out[31:16]), .en(and_4_out), .Q(resultS1), .clk(clock), .clr(Reset));

  assign s0 = {h1, h0};
  assign s1 = {h3, h2};
  assign s2 = {h5, h4};
  assign s3 = {h7, h6};
  assign s4 = {h9, h8};
  assign s5 = {h11, h10};
  assign s6 = {h13, h12};
  assign s7 = {h15, h14};

  // Other names for the same wires on the sheet: ftsel[3:0] = data[3:0]; fsselDATA[3:0] = data[7:4];
  //   fdsel[3:0] = data[11:8]; fpuop[2:0] = data[14:12]; smode = data[15]

  // Notes on the sheet:
  //   0.5
  //   x2
  //   i
  //   1.5
  //   x2 * y * y
endmodule
