// Logisim project mimo6.circ as structural Verilog: 13 circuits, main circuit MiMo_v05
// address
module MiMo_v05 (
  input  Cycle,
  input  Stop,
  input  Instr,
  input  [15:0] Addr,
  output [7:0] ucounter
);

  wire and_1_out, and_2_out, and_3_out, and_4_out, and_5_out, and_6_out, and_7_out, and_8_out, c, Clear_out,
       Clear_Screen_out, CLK, CLKIN, cont, FB_LED, gpio_1_o0, gpio_1_o1, gpio_1_o2, gpio_1_o3, gpio_1_o4,
       gpio_1_o5, gpio_1_o6, gpio_1_o7, gpio_2_o0, gpio_2_o1, gpio_2_o2, gpio_2_o3, gpio_2_o4, gpio_2_o5,
       gpio_2_o6, gpio_2_o7, GPIOASel, GPIOBSel, multiplexer_4_out, n, Ncmd, not_1_out, or_1_out, or_2_out,
       or_3_out, RAMSel, reset, RndSel, SYSSel, TTYSel, z;
  wire [1:0] addrsel, cond;
  wire [2:0] dregs, sregs, tregs;
  wire [3:0] aluop, icycles, showhexa_1_digit, showhexa_1_out_2, showhexa_1_out_3, showhexa_1_out_5,
       showhexa_2_digit, showhexa_2_out_2, showhexa_2_out_3, showhexa_2_out_5;
  wire [6:0] opcode;
  wire [7:0] adder_1_out, bit_extender_3_out, bit_extender_4_out, gpio_1_dout, gpio_2_dout,
       multiplexer_3_out, multiplexer_5_out;
  wire [15:0] address, aluout, bit_extender_1_out, bit_extender_2_out, cmds, controlled_buffer_2_out,
       controlled_buffer_4_out, cycles, data, dreg, DROM, frame_buffer_16x16_1_out_6,
       frame_buffer_16x16_1_out_7, frame_buffer_16x16_1_out_8, frame_buffer_16x16_1_out_9,
       frame_buffer_16x16_1_out_10, frame_buffer_16x16_1_out_11, frame_buffer_16x16_1_out_12,
       frame_buffer_16x16_1_out_13, frame_buffer_16x16_1_out_14, frame_buffer_16x16_1_out_15,
       frame_buffer_16x16_1_out_16, frame_buffer_16x16_1_out_17, frame_buffer_16x16_1_out_18,
       frame_buffer_16x16_1_out_19, frame_buffer_16x16_1_out_20, frame_buffer_16x16_1_out_21, immed, irreg,
       multiplexer_2_out, multiplexer_6_out, multiplexer_7_out, pcreg, registerfile_1_r0, registerfile_1_r1,
       registerfile_1_r2, registerfile_1_r3, registerfile_1_r4, registerfile_1_r5, registerfile_1_r6,
       registerfile_1_r7, sreg, treg;
  wire [31:4] CROM;

  Hex_Digit_Display hex_digit_display_1 (.value(showhexa_1_out_2));  // open: dp
  ShowHexa showhexa_1 (
    .Data(address), .Digit(showhexa_1_digit), .out_5(showhexa_1_out_5), .out_2(showhexa_1_out_2),
    .out_3(showhexa_1_out_3));
  RAM #(.addrWidth(14), .asyncread("true"), .dataWidth(16), .databus("bidir")) ram_1 (
    .addr(address[13:0]), .we(and_2_out), .oe(and_1_out), .clk(CLK));  // open: data
  nor nor_1 (Ncmd, ucounter[0], ucounter[1], ucounter[2], ucounter[3], ucounter[5], ucounter[6], ucounter[7], ucounter[4]);
  Hex_Digit_Display hex_digit_display_2 (.value(showhexa_1_digit));  // open: dp
  Hex_Digit_Display hex_digit_display_3 (.value(showhexa_1_out_3));  // open: dp
  and and_1 (and_1_out, RAMSel, not_1_out);
  not not_1 (not_1_out, CROM[6]);
  and and_2 (and_2_out, RAMSel, CROM[6]);
  Address_Decoder ADDR_DEC (
    .Address(address), .RAM(RAMSel), .FB_LED(FB_LED), .TTY(TTYSel), .SYS(SYSSel), .RND(RndSel),
    .GPIOA(GPIOASel), .GPIOB(GPIOBSel));
  // Probe on ucounter
  // Probe on ucounter
  Register Microcounter (.D(adder_1_out), .Q(ucounter), .clk(CLK), .clr(reset));  // open: en
  Clock SysClk (.out(CLKIN));
  Hex_Digit_Display hex_digit_display_4 (.value(showhexa_1_out_5));  // open: dp
  ROM #(.dataWidth(32)) rom_1 (.addr(ucounter), .data({CROM[31:20], cond, CROM[17:9], addrsel, CROM[6:4], aluop}));
  ROM #(.dataWidth(16)) rom_2 (.addr(ucounter), .data(DROM));
  Hex_Digit_Display hex_digit_display_5 (.value(showhexa_2_out_2));  // open: dp
  ShowHexa showhexa_2 (
    .Data(data), .Digit(showhexa_2_digit), .out_5(showhexa_2_out_5), .out_2(showhexa_2_out_2),
    .out_3(showhexa_2_out_3));
  // Probe on opcode
  // Probe on address
  Multiplexer #(.select(2), .width(16)) multiplexer_1 (
    .in0(pcreg), .in1(immed), .in2(aluout), .in3(sreg), .out(address), .sel(addrsel));
  Hex_Digit_Display hex_digit_display_6 (.value(showhexa_2_out_3));  // open: dp
  Hex_Digit_Display hex_digit_display_7 (.value(showhexa_2_digit));  // open: dp
  assign data = CROM[6] ? multiplexer_2_out : 16'bz;  // Controlled_Buffer controlled_buffer_1
  Multiplexer #(.select(2), .width(16)) multiplexer_2 (
    .in0(pcreg), .in1(dreg), .in2(treg), .in3(aluout), .out(multiplexer_2_out), .sel(CROM[22:21]));
  // Probe on CROM[22:21]
  or or_1 (or_1_out, z, n);
  // Probe on cond
  // Probe on addrsel
  Hex_Digit_Display hex_digit_display_8 (.value(showhexa_2_out_5));  // open: dp
  // Probe on DROM[7:0]
  Multiplexer #(.width(8)) multiplexer_3 (
    .in0(DROM[7:0]), .in1(DROM[15:8]), .out(multiplexer_3_out), .sel(multiplexer_4_out));
  // Probe on DROM[15:8]
  Multiplexer #(.select(2)) multiplexer_4 (
    .in0(z), .in1(or_1_out), .in2(n), .in3(c), .out(multiplexer_4_out), .sel(cond));
  Multiplexer #(.width(8)) multiplexer_5 (
    .in0({8{1'b0}}), .in1({1'b0, opcode}), .out(multiplexer_5_out), .sel(CROM[20]));
  // Probe on pcreg
  PC pc_1 (
    .imreg(immed), .sreg(sreg), .pcsel(CROM[10:9]), .pcload(CROM[11]), .clock(CLK), .reset(reset),
    .pcout(pcreg));
  // Probe on immed
  ImmediateReg immediatereg_1 (.IMLoad(CROM[14]), .CLKin(CLK), .DataIn(data), .ImmOut(immed));
  InstructionReg instructionreg_1 (
    .reset(reset), .irload(CROM[13]), .instruction(data), .clock(CLK), .dregsel(dregs), .sregsel(sregs),
    .tregsel(tregs), .opcode(opcode), .Instruction_register_Content(irreg));
  // Probe on irreg
  // Probe on opcode
  // Probe on adder_1_out
  Adder adder_1 (.a(multiplexer_3_out), .b(multiplexer_5_out), .out(adder_1_out));  // open: cin, cout
  // Probe on multiplexer_6_out
  Multiplexer #(.select(3), .width(16)) multiplexer_6 (
    .in0(data), .in1(immed), .in2(aluout), .in3(sreg), .in4(treg), .in5(pcreg), .in6({16{1'b0}}),
    .in7({16{1'b0}}), .out(multiplexer_6_out), .sel(CROM[17:15]));
  Button u_Reset (.out(reset));
  Registerfile registerfile_1 (
    .dsel(dregs), .regval(multiplexer_6_out), .dwrite(CROM[12]), .ssel(sregs), .swrite(CROM[23]),
    .tsel(tregs), .twrite(CROM[25]), .clock(CLK), .Reset(reset), .dreg(dreg), .sreg(sreg), .treg(treg),
    .r0(registerfile_1_r0), .r1(registerfile_1_r1), .r2(registerfile_1_r2), .r3(registerfile_1_r3),
    .r4(registerfile_1_r4), .r5(registerfile_1_r5), .r6(registerfile_1_r6), .r7(registerfile_1_r7));
  // Probe on sregs
  // Probe on dregs
  // Probe on ucounter
  // Probe on CROM[22:21]
  LED led_1 (.in(CROM[23]));
  Frame_Buffer_16x16 frame_buffer_16x16_1 (
    .address(address[3:0]), .store(and_3_out), .data(data), .clock(CLK), .reset(or_2_out),
    .out_6(frame_buffer_16x16_1_out_6), .out_7(frame_buffer_16x16_1_out_7),
    .out_8(frame_buffer_16x16_1_out_8), .out_9(frame_buffer_16x16_1_out_9),
    .out_10(frame_buffer_16x16_1_out_10), .out_11(frame_buffer_16x16_1_out_11),
    .out_12(frame_buffer_16x16_1_out_12), .out_13(frame_buffer_16x16_1_out_13),
    .out_14(frame_buffer_16x16_1_out_14), .out_15(frame_buffer_16x16_1_out_15),
    .out_16(frame_buffer_16x16_1_out_16), .out_17(frame_buffer_16x16_1_out_17),
    .out_18(frame_buffer_16x16_1_out_18), .out_19(frame_buffer_16x16_1_out_19),
    .out_20(frame_buffer_16x16_1_out_20), .out_21(frame_buffer_16x16_1_out_21));
  and and_3 (and_3_out, FB_LED, CROM[6]);
  // Probe on registerfile_1_r0
  // Probe on registerfile_1_r1
  // Probe on registerfile_1_r2
  // Probe on registerfile_1_r3
  // Probe on registerfile_1_r4
  // Probe on registerfile_1_r5
  // Probe on registerfile_1_r6
  // Probe on registerfile_1_r7
  // Probe on dreg
  // Probe on sreg
  // Probe on treg
  // Probe on tregs
  // Probe on cond
  LED led_2 (.in(CROM[20]));
  DotMatrix #(.inputtype("row"), .matrixcols(16), .matrixrows(16)) dotmatrix_1 (
    .row0(frame_buffer_16x16_1_out_21), .row1(frame_buffer_16x16_1_out_20),
    .row2(frame_buffer_16x16_1_out_19), .row3(frame_buffer_16x16_1_out_18),
    .row4(frame_buffer_16x16_1_out_17), .row5(frame_buffer_16x16_1_out_16),
    .row6(frame_buffer_16x16_1_out_15), .row7(frame_buffer_16x16_1_out_14),
    .row8(frame_buffer_16x16_1_out_13), .row9(frame_buffer_16x16_1_out_12),
    .row10(frame_buffer_16x16_1_out_11), .row11(frame_buffer_16x16_1_out_10),
    .row12(frame_buffer_16x16_1_out_9), .row13(frame_buffer_16x16_1_out_8),
    .row14(frame_buffer_16x16_1_out_7), .row15(frame_buffer_16x16_1_out_6));
  Counters counters_1 (
    .new_ucounter(adder_1_out), .reset(reset), .clock(CLK), .cmds(cmds), .cycles(cycles), .icycles(icycles));
  Multiplexer #(.select(2), .width(16)) multiplexer_7 (
    .in0(treg), .in1(immed), .in2({16{1'b0}}), .in3(16'h1), .out(multiplexer_7_out), .sel(CROM[5:4]));
  // Probe on CROM[5:4]
  // Probe on CROM[17:15]
  LED led_3 (.in(CROM[14]));
  or or_2 (or_2_out, reset, Clear_out);
  Button Clear (.out(Clear_out));
  Button u_Cont (.out(cont));
  // Probe on {CROM[31:20], cond, CROM[17:9], addrsel, CROM[6:4], aluop}
  LED led_4 (.in(CROM[12]));
  LED led_5 (.in(CROM[13]));
  DebugUnit debugunit_1 (
    .reset(reset), .\continue (cont), .clock(CLKIN), .pcreg(pcreg), .break_addr(Addr), .break_on_addr(Stop),
    .ucounter(ucounter), .break_on_instr(Instr), .break_on_cycle(Cycle), .clock_out(CLK));
  ALU alu_1 (
    .A(sreg), .B(multiplexer_7_out), .rst(reset), .aluop(aluop), .sf(CROM[24]), .clk(CLK),
    .withcarry(CROM[26]), .Carry(c), .Zero(z), .Negative(n), .Result(aluout));
  // Probe on aluout
  // Probe on icycles
  // Probe on CROM[10:9]
  LED led_6 (.in(CROM[11]));
  // Probe on opcode
  LED u_C (.in(c));
  LED u_Z (.in(z));
  LED u_N (.in(n));
  // Probe on cycles
  // Probe on addrsel
  LED led_7 (.in(CROM[6]));
  // Probe on tregs
  // Probe on sregs
  // Probe on address
  // Probe on pcreg
  // Probe on irreg
  // Probe on immed
  // Probe on aluout
  LED New_CMD (.in(Ncmd));
  // Probe on DROM
  // Probe on CROM[5:4]
  // Probe on irreg
  // Probe on dregs
  // Probe on data
  // Probe on cmds
  // Probe on aluop
  TTY #(.cols(60), .rows(20)) tty_1 (.data(data[6:0]), .clk(CLK), .we(and_4_out), .clr(or_3_out));
  and and_4 (and_4_out, TTYSel, CROM[6]);
  or or_3 (or_3_out, reset, Clear_Screen_out);
  Button Clear_Screen (.out(Clear_Screen_out));
  assign bit_extender_1_out = {{8{1'b0}}, gpio_1_dout};  // Bit_Extender bit_extender_1
  and and_5 (and_5_out, GPIOASel, CROM[6]);
  and and_6 (and_6_out, ~CROM[6], GPIOASel);  // AND_Gate
  assign bit_extender_2_out = {{8{1'b0}}, gpio_2_dout};  // Bit_Extender bit_extender_2
  and and_7 (and_7_out, GPIOBSel, CROM[6]);
  and and_8 (and_8_out, ~CROM[6], GPIOBSel);  // AND_Gate
  Bit_Extender #(.in_width(16), .out_width(8), .\type ("zero")) bit_extender_3 (
    .in(controlled_buffer_2_out), .out(bit_extender_3_out));
  assign controlled_buffer_2_out = and_5_out ? data : 16'bz;  // Controlled_Buffer controlled_buffer_2
  assign data = and_6_out ? bit_extender_1_out : 16'bz;  // Controlled_Buffer controlled_buffer_3
  Bit_Extender #(.in_width(16), .out_width(8), .\type ("zero")) bit_extender_4 (
    .in(controlled_buffer_4_out), .out(bit_extender_4_out));
  assign controlled_buffer_4_out = and_7_out ? data : 16'bz;  // Controlled_Buffer controlled_buffer_4
  assign data = and_8_out ? bit_extender_2_out : 16'bz;  // Controlled_Buffer controlled_buffer_5
  GPIO gpio_1 (
    .DIN(bit_extender_3_out), .RST(reset), .WE(and_5_out), .Address(address[2:0]), .I0(gpio_1_o0),
    .I1(gpio_1_o1), .I2(gpio_1_o2), .I3(gpio_1_o3), .I4(gpio_1_o4), .I5(gpio_1_o5), .I6(gpio_1_o6),
    .I7(gpio_1_o7), .DOUT(gpio_1_dout), .O0(gpio_1_o0), .O1(gpio_1_o1), .O2(gpio_1_o2), .O3(gpio_1_o3),
    .O4(gpio_1_o4), .O5(gpio_1_o5), .O6(gpio_1_o6), .O7(gpio_1_o7));
  GPIO gpio_2 (
    .DIN(bit_extender_4_out), .RST(reset), .WE(and_7_out), .Address(address[2:0]), .I0(gpio_2_o0),
    .I1(gpio_2_o1), .I2(gpio_2_o2), .I3(gpio_2_o3), .I4(gpio_2_o4), .I5(gpio_2_o5), .I6(gpio_2_o6),
    .I7(gpio_2_o7), .DOUT(gpio_2_dout), .O0(gpio_2_o0), .O1(gpio_2_o1), .O2(gpio_2_o2), .O3(gpio_2_o3),
    .O4(gpio_2_o4), .O5(gpio_2_o5), .O6(gpio_2_o6), .O7(gpio_2_o7));

  // Other names for the same wires on the sheet: CROM (some bits) = {cond, addrsel, aluop}; op2sel[1:0] = CROM[5:4];
  //   datawrite = CROM[6]; pcsel[1:0] = CROM[10:9]; pcload = CROM[11]; dwrite = CROM[12]; irload = CROM[13];
  //   imload = CROM[14]; regsrc[2:0] = CROM[17:15]; indexsel = CROM[20]; datasel[1:0] = CROM[22:21];
  //   swrite = CROM[23]; flags = CROM[24]; twrite = CROM[25]; withcarry = CROM[26]; dbgadr = Stop; dbgcyc = Cycle;
  //   dbgins = Instr; MicroPC[7:0] = ucounter

  // Notes on the sheet:
  //   Based on: http://minnie.tuhs.org/Programs/UcodeCPU/index.html
  //   v05: Migration to EVO, Debug, Counters, ImmReg Units
  //   v05a: norz instead of corz
  //   Address BUS
  //   RAM
  //   Microcode Control Unit
  //   contents of rom_1 (hex, n*v repeats v):
  //   2000 100800 19000 1800 1011000 4800 1011001 4800 1011002 4800 1011003 4800 1011004 4800 1011005 4800
  //   1011006 4800 1011007 4800 1011008 4800 1011009 4800 101100a 4800 101100b 4800 101100c 4800 101100d
  //   4800 101100e 4800 101100f 4800 e00 10*4800 1000001 4800 1000005 4800 4800 29e00 4800 1180 4800 1100
  //   4800 2001c0 4800 200140 1180 810031 1011030 1011031 1000001 1000001 1180 810031 4180 5011000 5011001
  //   5011020 5011021 54*0 1011010 1011011 1011012 1011013 1011014 1011015 1011016 1011017 1011018 1011019
  //   101101a 101101b 101101c 101101d 101101e 101101f a00 c00 1010011 1010015 29a00 1080 2000c0 1110
  //   200150 810030 0 0 80000 80000 c0000 c0000 c0000 0 c0000 0 c0000 c0000 19000 21000 810030 2000180
  //   810030 4001c0 810031 2001c0 810030 a00
  //   contents of rom_2 (hex, n*v repeats v):
  //   101 202 0 0 0 8080 0 8181 0 8282 0 8383 0 8484 0 8585 0 8686 0 8787 0 8888 0 8989 0 8a8a 0 8b8b 0
  //   8c8c 0 8d8d 0 8e8e 0 8f8f 0 9090 9191 9a9a 9b9b 9c9c 9d9d 9e9e 9f9f a0a0 a2a2 0 9292 0 9393 9494 0
  //   9595 0 9797 0 9696 0 9898 0 9999 3a3a 0 0 a4a4 a5a5 a8a8 abab aeae 84*0 9100 91 9100 91 9100 91 a100
  //   91 a391 9100 a6a7 a7a6 0 0 a9a9 aaaa 0 acac adad 0 afaf
  //   MiMo - Microprogrammed CPU Model
  //   Control ROM
  //   Address of third uinstruction is "opcode+2"
  //   Decision ROM
  //   Data BUS
  //   v0.5a OR EVO
  //   PC
  //   ImmReg
  //   InsReg
  //   Quick tips:
  //   Use ctrl+t to manually toggle global clock signal
  //   Registers
  //   Use Simulate->Ticks Enabled for automatic clock signal
  //   Debug
  //   Frame Buffer LED 16x16
  //   Micro Instruction
  //   ALU
  //   Instruction:
  //   Flags
  //   Status
  //   Address, Data Bus
  //   Spec. Registers
  //   TTY
  //   GPIOA
  //   GPIOB
endmodule

module InstructionReg (
  input  [15:0] instruction,
  input  reset,
  input  clock,
  input  irload,
  output [2:0] dregsel,
  output [2:0] sregsel,
  output [2:0] tregsel,
  output [6:0] opcode,
  output [15:0] Instruction_register_Content
);

  Register #(.width(16)) register_1 (
    .D(instruction), .en(irload), .Q({Instruction_register_Content[15:3], dregsel}), .clk(clock), .clr(reset));

  assign Instruction_register_Content[2:0] = dregsel;
  assign opcode = Instruction_register_Content[15:9];
  assign sregsel = Instruction_register_Content[5:3];
  assign tregsel = Instruction_register_Content[8:6];

  // Notes on the sheet:
  //   IR Logic
endmodule

module Registerfile (
  input  [15:0] regval,
  input  Reset,
  input  clock,
  input  dwrite,
  input  swrite,
  input  twrite,
  input  [2:0] dsel,
  input  [2:0] ssel,
  input  [2:0] tsel,
  output [15:0] r0,
  output [15:0] r1,
  output [15:0] r2,
  output [15:0] r3,
  output [15:0] r4,
  output [15:0] r5,
  output [15:0] r6,
  output [15:0] r7,
  output [15:0] dreg,
  output [15:0] sreg,
  output [15:0] treg
);

  wire demultiplexer_1_out0, demultiplexer_1_out1, demultiplexer_1_out2, demultiplexer_1_out3,
       demultiplexer_1_out4, demultiplexer_1_out5, demultiplexer_1_out6, demultiplexer_1_out7;

  Demultiplexer #(.select(3)) demultiplexer_1 (
    .out0(demultiplexer_1_out0), .out1(demultiplexer_1_out1), .out2(demultiplexer_1_out2),
    .out3(demultiplexer_1_out3), .out4(demultiplexer_1_out4), .out5(demultiplexer_1_out5),
    .out6(demultiplexer_1_out6), .out7(demultiplexer_1_out7), .in(dwrite), .sel(dsel));
  Demultiplexer #(.select(3)) demultiplexer_2 (
    .out0(demultiplexer_1_out0), .out1(demultiplexer_1_out1), .out2(demultiplexer_1_out2),
    .out3(demultiplexer_1_out3), .out4(demultiplexer_1_out4), .out5(demultiplexer_1_out5),
    .out6(demultiplexer_1_out6), .out7(demultiplexer_1_out7), .in(swrite), .sel(ssel));
  Demultiplexer #(.select(3)) demultiplexer_3 (
    .out0(demultiplexer_1_out0), .out1(demultiplexer_1_out1), .out2(demultiplexer_1_out2),
    .out3(demultiplexer_1_out3), .out4(demultiplexer_1_out4), .out5(demultiplexer_1_out5),
    .out6(demultiplexer_1_out6), .out7(demultiplexer_1_out7), .in(twrite), .sel(tsel));
  Register #(.width(16)) register_1 (.D(regval), .en(demultiplexer_1_out0), .Q(r0), .clk(clock), .clr(Reset));
  Register #(.width(16)) register_2 (.D(regval), .en(demultiplexer_1_out1), .Q(r1), .clk(clock), .clr(Reset));
  Register #(.width(16)) register_3 (.D(regval), .en(demultiplexer_1_out2), .Q(r2), .clk(clock), .clr(Reset));
  Register #(.width(16)) register_4 (.D(regval), .en(demultiplexer_1_out3), .Q(r3), .clk(clock), .clr(Reset));
  Register #(.width(16)) register_5 (.D(regval), .en(demultiplexer_1_out4), .Q(r4), .clk(clock), .clr(Reset));
  Register #(.width(16)) register_6 (.D(regval), .en(demultiplexer_1_out5), .Q(r5), .clk(clock), .clr(Reset));
  Register #(.width(16)) register_7 (.D(regval), .en(demultiplexer_1_out6), .Q(r6), .clk(clock), .clr(Reset));
  Register #(.width(16)) register_8 (.D(regval), .en(demultiplexer_1_out7), .Q(r7), .clk(clock), .clr(Reset));
  Multiplexer #(.select(3), .width(16)) multiplexer_1 (
    .in0(r0), .in1(r1), .in2(r2), .in3(r3), .in4(r4), .in5(r5), .in6(r6), .in7(r7), .out(dreg), .sel(dsel));
  Multiplexer #(.select(3), .width(16)) multiplexer_2 (
    .in0(r0), .in1(r1), .in2(r2), .in3(r3), .in4(r4), .in5(r5), .in6(r6), .in7(r7), .out(sreg), .sel(ssel));
  Multiplexer #(.select(3), .width(16)) multiplexer_3 (
    .in0(r0), .in1(r1), .in2(r2), .in3(r3), .in4(r4), .in5(r5), .in6(r6), .in7(r7), .out(treg), .sel(tsel));

  // Notes on the sheet:
  //   Register File
endmodule

module ALU (
  input  [15:0] A,
  input  [15:0] B,
  input  withcarry,
  input  rst,
  input  sf,
  input  clk,
  input  [3:0] aluop,
  output Carry,
  output Zero,
  output Negative,
  output [15:0] Result
);

  wire adder_1_cout, and_2_out, C, or_2_out, subtractor_1_bout, useC, z;
  wire [15:0] adder_1_out, and_1_out, divider_1_out, divider_1_rem, multiplier_1_out, nand_1_out, nor_1_out,
       not_1_out, or_1_out, shifter_1_out, shifter_2_out, shifter_3_out, shifter_4_out, shifter_5_out,
       subtractor_1_out, xor_1_out;

  Adder #(.width(16)) adder_1 (.a(A), .b(B), .out(adder_1_out), .cin(useC), .cout(adder_1_cout));
  Subtractor #(.width(16)) subtractor_1 (.a(A), .b(B), .out(subtractor_1_out), .bin(useC), .bout(subtractor_1_bout));
  Multiplier #(.width(16)) multiplier_1 (.a(A), .b(B), .out(multiplier_1_out), .cin({16{1'b0}}));  // open: cout
  Divider #(.width(16)) divider_1 (.a(A), .b(B), .out(divider_1_out), .upper({16{1'b0}}), .rem(divider_1_rem));
  assign and_1_out = A & B;  // AND_Gate and_1, 16 bits wide
  assign or_1_out = A | B;  // OR_Gate or_1, 16 bits wide
  assign xor_1_out = A ^ B;  // XOR_Gate xor_1, 16 bits wide
  assign nand_1_out = ~(A & B);  // NAND_Gate nand_1, 16 bits wide
  assign nor_1_out = ~(A | B);  // NOR_Gate nor_1, 16 bits wide
  assign not_1_out = ~A;  // NOT_Gate not_1, 16 bits wide
  Shifter #(.width(16)) shifter_1 (.in(A), .\dist (B[3:0]), .out(shifter_1_out));
  Shifter #(.shift("lr"), .width(16)) shifter_2 (.in(A), .\dist (B[3:0]), .out(shifter_2_out));
  Shifter #(.shift("ar"), .width(16)) shifter_3 (.in(A), .\dist (B[3:0]), .out(shifter_3_out));
  Shifter #(.shift("rl"), .width(16)) shifter_4 (.in(A), .\dist (B[3:0]), .out(shifter_4_out));
  Shifter #(.shift("rr"), .width(16)) shifter_5 (.in(A), .\dist (B[3:0]), .out(shifter_5_out));
  Multiplexer #(.select(4), .width(16)) multiplexer_1 (
    .in0(adder_1_out), .in1(subtractor_1_out), .in2(multiplier_1_out), .in3(divider_1_out),
    .in4(divider_1_rem), .in5(and_1_out), .in6(or_1_out), .in7(xor_1_out), .in8(nand_1_out), .in9(nor_1_out),
    .in10(not_1_out), .in11(shifter_1_out), .in12(shifter_2_out), .in13(shifter_3_out), .in14(shifter_4_out),
    .in15(shifter_5_out), .out(Result), .sel(aluop));
  Multiplexer #(.select(4)) multiplexer_2 (
    .in0(adder_1_cout), .in1(subtractor_1_bout), .in2(1'b0), .in3(1'b0), .in4(1'b0), .in5(1'b0), .in6(1'b0),
    .in7(1'b0), .in8(1'b0), .in9(1'b0), .in10(1'b0), .in11(1'b0), .in12(1'b0), .in13(1'b0), .in14(1'b0),
    .in15(1'b0), .out(C), .sel(aluop));
  or or_2 (or_2_out, Result[0], Result[1], Result[2], Result[3], Result[4], Result[5], Result[6], Result[7], Result[9], Result[10], Result[11], Result[12], Result[13], Result[14], Result[15], Result[8]);
  not not_2 (z, or_2_out);
  and and_2 (and_2_out, sf, clk);
  D_Flip_Flop d_ff_1 (.D(C), .clk(and_2_out), .Q(Carry), .reset(rst));  // open: Qn, preset
  D_Flip_Flop d_ff_2 (.D(z), .clk(and_2_out), .Q(Zero), .reset(rst));  // open: Qn, preset
  D_Flip_Flop d_ff_3 (.D(Result[15]), .clk(and_2_out), .Q(Negative), .reset(rst));  // open: Qn, preset
  and and_3 (useC, withcarry, Carry);

  // Other names for the same wires on the sheet: n = Result[15]

  // Notes on the sheet:
  //   16-bit ALU
endmodule

module PC (
  input  [15:0] imreg,
  input  pcload,
  input  clock,
  input  reset,
  input  [15:0] sreg,
  input  [1:0] pcsel,
  output [15:0] pcout
);

  wire [15:0] adder_1_out, adder_2_out, multiplexer_1_out;

  Adder #(.width(16)) adder_1 (.a(pcout), .b(16'h1), .out(adder_1_out));  // open: cin, cout
  Adder #(.width(16)) adder_2 (.a(pcout), .b(imreg), .out(adder_2_out));  // open: cin, cout
  Multiplexer #(.select(2), .width(16)) multiplexer_1 (
    .in0(adder_1_out), .in1(imreg), .in2(adder_2_out), .in3(sreg), .out(multiplexer_1_out), .sel(pcsel));
  Register #(.width(16)) register_1 (.D(multiplexer_1_out), .en(pcload), .Q(pcout), .clk(clock), .clr(reset));

  // Notes on the sheet:
  //   PC Logic
endmodule

module ShowHexa (
  input  [15:0] Data,
  output [3:0] out_2,
  output [3:0] out_3,
  output [3:0] Digit,
  output [3:0] out_5
);


  assign Digit = Data[7:4];
  assign out_2 = Data[15:12];
  assign out_3 = Data[11:8];
  assign out_5 = Data[3:0];
endmodule

module Frame_Buffer_16x16 (
  input  [3:0] address,
  input  store,
  input  [15:0] data,
  input  clock,
  input  reset,
  output [15:0] out_6,
  output [15:0] out_7,
  output [15:0] out_8,
  output [15:0] out_9,
  output [15:0] out_10,
  output [15:0] out_11,
  output [15:0] out_12,
  output [15:0] out_13,
  output [15:0] out_14,
  output [15:0] out_15,
  output [15:0] out_16,
  output [15:0] out_17,
  output [15:0] out_18,
  output [15:0] out_19,
  output [15:0] out_20,
  output [15:0] out_21
);

  wire demultiplexer_1_out0, demultiplexer_1_out1, demultiplexer_1_out2, demultiplexer_1_out3,
       demultiplexer_1_out4, demultiplexer_1_out5, demultiplexer_1_out6, demultiplexer_1_out7,
       demultiplexer_1_out8, demultiplexer_1_out9, demultiplexer_1_out10, demultiplexer_1_out11,
       demultiplexer_1_out12, demultiplexer_1_out13, demultiplexer_1_out14, demultiplexer_1_out15;

  Demultiplexer #(.select(4)) demultiplexer_1 (
    .out0(demultiplexer_1_out0), .out1(demultiplexer_1_out1), .out2(demultiplexer_1_out2),
    .out3(demultiplexer_1_out3), .out4(demultiplexer_1_out4), .out5(demultiplexer_1_out5),
    .out6(demultiplexer_1_out6), .out7(demultiplexer_1_out7), .out8(demultiplexer_1_out8),
    .out9(demultiplexer_1_out9), .out10(demultiplexer_1_out10), .out11(demultiplexer_1_out11),
    .out12(demultiplexer_1_out12), .out13(demultiplexer_1_out13), .out14(demultiplexer_1_out14),
    .out15(demultiplexer_1_out15), .in(store), .sel(address));
  Register #(.width(16)) register_1 (.D(data), .en(demultiplexer_1_out0), .Q(out_6), .clk(clock), .clr(reset));
  Register #(.width(16)) register_2 (.D(data), .en(demultiplexer_1_out1), .Q(out_7), .clk(clock), .clr(reset));
  Register #(.width(16)) register_3 (.D(data), .en(demultiplexer_1_out2), .Q(out_8), .clk(clock), .clr(reset));
  Register #(.width(16)) register_4 (.D(data), .en(demultiplexer_1_out3), .Q(out_9), .clk(clock), .clr(reset));
  Register #(.width(16)) register_5 (.D(data), .en(demultiplexer_1_out4), .Q(out_10), .clk(clock), .clr(reset));
  Register #(.width(16)) register_6 (.D(data), .en(demultiplexer_1_out5), .Q(out_11), .clk(clock), .clr(reset));
  Register #(.width(16)) register_7 (.D(data), .en(demultiplexer_1_out6), .Q(out_12), .clk(clock), .clr(reset));
  Register #(.width(16)) register_8 (.D(data), .en(demultiplexer_1_out7), .Q(out_13), .clk(clock), .clr(reset));
  Register #(.width(16)) register_9 (.D(data), .en(demultiplexer_1_out8), .Q(out_14), .clk(clock), .clr(reset));
  Register #(.width(16)) register_10 (.D(data), .en(demultiplexer_1_out9), .Q(out_15), .clk(clock), .clr(reset));
  Register #(.width(16)) register_11 (.D(data), .en(demultiplexer_1_out10), .Q(out_16), .clk(clock), .clr(reset));
  Register #(.width(16)) register_12 (.D(data), .en(demultiplexer_1_out11), .Q(out_17), .clk(clock), .clr(reset));
  Register #(.width(16)) register_13 (.D(data), .en(demultiplexer_1_out12), .Q(out_18), .clk(clock), .clr(reset));
  Register #(.width(16)) register_14 (.D(data), .en(demultiplexer_1_out13), .Q(out_19), .clk(clock), .clr(reset));
  Register #(.width(16)) register_15 (.D(data), .en(demultiplexer_1_out14), .Q(out_20), .clk(clock), .clr(reset));
  Register #(.width(16)) register_16 (.D(data), .en(demultiplexer_1_out15), .Q(out_21), .clk(clock), .clr(reset));
endmodule

module Address_Decoder (
  input  [15:0] Address,
  output RAM,
  output FB_LED,
  output TTY,
  output SYS,
  output RND,
  output GPIOA,
  output GPIOB
);

  wire and_1_out, decoder_1_out1, decoder_2_out0, decoder_2_out1, decoder_2_out2, decoder_2_out3, nor_1_out;

  Decoder #(.enable("false"), .select(2)) decoder_1 (
    .out0(RAM), .out1(decoder_1_out1), .out2(FB_LED), .out3(TTY), .sel(Address[15:14]));
  nor nor_1 (nor_1_out, Address[6], Address[7], Address[8], Address[9], Address[11], Address[12], Address[13], Address[10]);
  and and_1 (and_1_out, decoder_1_out1, nor_1_out);
  Decoder #(.select(3)) decoder_2 (
    .out0(decoder_2_out0), .out1(decoder_2_out1), .out2(decoder_2_out2), .out3(decoder_2_out3), .out4(RND),
    .out5(GPIOA), .out6(GPIOB), .sel(Address[5:3]), .en(and_1_out));  // open: out7
  or or_1 (SYS, decoder_2_out1, decoder_2_out0, decoder_2_out2, decoder_2_out3);
endmodule

module Counters (
  input  [7:0] new_ucounter,
  input  reset,
  input  clock,
  output [15:0] cycles,
  output [3:0] icycles,
  output [15:0] cmds
);

  wire nor_1_out;

  nor nor_1 (nor_1_out, new_ucounter[7], new_ucounter[6], new_ucounter[5], new_ucounter[4], new_ucounter[2], new_ucounter[1], new_ucounter[0], new_ucounter[3]);
  Counter #(.max('hffff), .width(16)) counter_1 (
    .Q(cycles), .clk(clock), .clr(reset));  // open: load, D, count, carry, up
  Counter #(.max('hf), .width(4)) counter_2 (
    .load(nor_1_out), .D(4'b0000), .Q(icycles), .clk(clock), .clr(reset));  // open: count, carry, up
  Counter #(.max('hffff), .width(16)) counter_3 (
    .count(nor_1_out), .Q(cmds), .clk(clock), .clr(reset));  // open: load, D, carry, up
  // Probe on cycles
  // Probe on icycles
  // Probe on cmds

  // Notes on the sheet:
  //   Counts the number of clock cycles
  //   since the start.
  //   Counts the number of clock cycles
  //   since the start of current instruction.
  //   Counts the number of instructions
  //   since the start.
  //   Cycle/Cmds Counters
endmodule

module DebugUnit (
  input  reset,
  input  \continue ,
  input  clock,
  input  [15:0] pcreg,
  input  [15:0] break_addr,
  input  break_on_addr,
  input  [7:0] ucounter,
  input  break_on_instr,
  input  break_on_cycle,
  output clock_out
);

  wire and_1_out, and_2_out, and_3_out, nor_1_out, nor_2_out, nor_3_out, or_1_out, shift_register_1_out,
       shift_register_1_q0;
  wire [15:0] xor_1_out;

  Shift_Register #(.length(2), .trigger("falling")) shift_register_1 (
    .in(\continue ), .clk(clock), .out(shift_register_1_out), .clr(reset), .q0(shift_register_1_q0));  // open: shift, load, d0, d1, q1
  assign xor_1_out = pcreg ^ break_addr;  // XOR_Gate xor_1, 16 bits wide
  LED Addr (.in(break_on_addr));
  and and_1 (and_1_out, ~shift_register_1_out, shift_register_1_q0);  // AND_Gate
  nor nor_1 (nor_1_out, xor_1_out[15], xor_1_out[14], xor_1_out[13], xor_1_out[12], xor_1_out[11], xor_1_out[10], xor_1_out[9], xor_1_out[8], xor_1_out[6], xor_1_out[5], xor_1_out[4], xor_1_out[3], xor_1_out[2], xor_1_out[1], xor_1_out[0], xor_1_out[7]);
  and and_2 (and_2_out, nor_1_out, break_on_addr, nor_2_out);
  nor nor_2 (nor_2_out, ucounter[7], ucounter[6], ucounter[5], ucounter[4], ucounter[2], ucounter[1], ucounter[0], ucounter[3]);
  and and_3 (and_3_out, nor_2_out, break_on_instr);
  LED Instr (.in(break_on_instr));
  LED Cycle (.in(break_on_cycle));
  nor nor_3 (nor_3_out, and_2_out, and_3_out, break_on_cycle);
  or or_1 (or_1_out, and_1_out, nor_3_out);
  LED Pass (.in(or_1_out));
  and and_4 (clock_out, clock, or_1_out);

  // Notes on the sheet:
  //   Breaks on PC = break_addr
  //   Breaks on each new instruction
  //   Breaks on each clock pulse
  //   Makes sure the 'continue' button only
  //   lets through 1 clock pulse, until you let go
  //   and press it again.
  //   Outputs 1 only on first cycle (shift bits are unequal).
  //   Debug Unit
  //   PC = break_addr?
endmodule

module ImmediateReg (
  input  [15:0] DataIn,
  input  IMLoad,
  input  CLKin,
  output [15:0] ImmOut
);

  Register #(.width(16)) register_1 (.D(DataIn), .en(IMLoad), .Q(ImmOut), .clk(CLKin));  // open: clr
  // Probe on ImmOut
endmodule

module GPIO (
  input  [7:0] DIN,
  input  I0,
  input  I1,
  input  I2,
  input  I3,
  input  I4,
  input  I5,
  input  I6,
  input  I7,
  input  RST,
  input  WE,
  input  [2:0] Address,
  output O0,
  output O1,
  output O2,
  output O3,
  output O4,
  output O5,
  output O6,
  output O7,
  output [7:0] DOUT
);

  IOCell iocell_1 (.DIN(DIN[0]), .WE(WE), .Address(Address), .Reset(RST), .xi(I0), .xo(O0), .DOUT(DOUT[0]));
  IOCell iocell_2 (.DIN(DIN[1]), .WE(WE), .Address(Address), .Reset(RST), .xi(I1), .xo(O1), .DOUT(DOUT[1]));
  IOCell iocell_3 (.DIN(DIN[2]), .WE(WE), .Address(Address), .Reset(RST), .xi(I2), .xo(O2), .DOUT(DOUT[2]));
  IOCell iocell_4 (.DIN(DIN[3]), .WE(WE), .Address(Address), .Reset(RST), .xi(I3), .xo(O3), .DOUT(DOUT[3]));
  IOCell iocell_5 (.DIN(DIN[4]), .WE(WE), .Address(Address), .Reset(RST), .xi(I4), .xo(O4), .DOUT(DOUT[4]));
  IOCell iocell_6 (.DIN(DIN[5]), .WE(WE), .Address(Address), .Reset(RST), .xi(I5), .xo(O5), .DOUT(DOUT[5]));
  IOCell iocell_7 (.DIN(DIN[6]), .WE(WE), .Address(Address), .Reset(RST), .xi(I6), .xo(O6), .DOUT(DOUT[6]));
  IOCell iocell_8 (.DIN(DIN[7]), .WE(WE), .Address(Address), .Reset(RST), .xi(I7), .xo(O7), .DOUT(DOUT[7]));
endmodule

module IOCell (
  input  DIN,
  input  Reset,
  input  xi,
  input  WE,
  input  [2:0] Address,
  output xo,
  output DOUT
);

  wire and_1_out, and_2_out, and_5_out, clock_1_out, Clr, controlled_buffer_1_out, d_ff_1_q, d_ff_2_q,
       d_ff_2_qn, d_ff_3_q, decoder_1_out0, decoder_1_out2, Set, WEC;

  and and_1 (and_1_out, WEC, DIN, Address[2]);
  and and_2 (and_2_out, and_1_out, ~Address[0]);  // AND_Gate
  and and_3 (Set, and_1_out, Address[0]);
  Clock clock_1 (.out(clock_1_out));
  or or_1 (Clr, Reset, and_2_out);
  and and_4 (WEC, WE, clock_1_out);
  Decoder #(.select(2)) decoder_1 (
    .out0(decoder_1_out0), .out2(decoder_1_out2), .sel(Address[1:0]), .en(and_5_out));  // open: out1, out3
  and and_5 (and_5_out, WEC, ~Address[2]);  // AND_Gate
  D_Flip_Flop d_ff_1 (.D(DIN), .clk(decoder_1_out2), .Q(d_ff_1_q), .preset(Set), .reset(Clr));  // open: Qn
  D_Flip_Flop d_ff_2 (.D(DIN), .clk(decoder_1_out0), .Q(d_ff_2_q), .Qn(d_ff_2_qn), .reset(Reset));  // open: preset
  assign controlled_buffer_1_out = d_ff_2_qn ? xi : 1'bz;  // Controlled_Buffer controlled_buffer_1
  D_Flip_Flop #(.trigger("falling")) d_ff_3 (
    .D(controlled_buffer_1_out), .clk(clock_1_out), .Q(d_ff_3_q));  // open: Qn, preset, reset
  assign xo = d_ff_2_q ? d_ff_1_q : 1'bz;  // Controlled_Buffer controlled_buffer_2
  Multiplexer #(.select(3)) multiplexer_1 (
    .in0(d_ff_2_q), .in1(d_ff_3_q), .in2(d_ff_1_q), .in3(1'b0), .in4(1'b0), .in5(1'b0), .in6(1'b0),
    .in7(1'b0), .out(DOUT), .sel(Address));

  // Other names for the same wires on the sheet: A0 = Address[0]; AL[1:0] = Address[1:0]; A2 = Address[2];
  //   Rst = Reset
endmodule
