// Logisim project Grohar_RGB_Joystick_IO.circ as structural Verilog: 2 circuits, main circuit main
module main (
);

  wire CLK, datawrite, GPIO, reset;
  wire [3:0] joystick_1_x, joystick_1_y;
  wire [15:0] address, data, joy_dout;

  Joystick joystick_1 (.x(joystick_1_x), .y(joystick_1_y));
  Joy joy_1 (
    .addr(address), .din(data), .wr(datawrite), .cs(GPIO), .clk(CLK), .rst(reset), .joystick_x(joystick_1_x),
    .joystick_y(joystick_1_y), .dout(joy_dout));
endmodule

module Joy (
  input  [15:0] addr,
  input  [15:0] din,
  input  wr,
  input  cs,
  input  clk,
  input  rst,
  input  [3:0] joystick_x,
  input  [3:0] joystick_y,
  output [15:0] dout
);

  wire and_1_out, decoder_1_out0, not_1_out, or_1_out;
  wire [15:0] bit_extender_1_out, bit_extender_2_out, ctrl_q, reg_x_q, reg_y_q;

  or or_1 (or_1_out, rst, not_1_out);
  not not_1 (not_1_out, ctrl_q[0]);
  assign bit_extender_1_out = {{12{1'b0}}, joystick_x};  // Bit_Extender bit_extender_1
  Decoder #(.enable("false"), .select(2)) decoder_1 (.out0(decoder_1_out0), .sel(addr[1:0]));  // open: out1, out2, out3
  assign bit_extender_2_out = {{12{1'b0}}, joystick_y};  // Bit_Extender bit_extender_2
  Register #(.width(16)) ctrl (.D(din), .en(and_1_out), .clk(clk), .Q(ctrl_q), .clr(rst));
  and and_1 (and_1_out, decoder_1_out0, wr, cs);
  Register #(.width(16)) reg_x (.D(bit_extender_1_out), .en(ctrl_q[0]), .clk(clk), .Q(reg_x_q), .clr(or_1_out));
  Register #(.width(16)) reg_y (.D(bit_extender_2_out), .en(ctrl_q[0]), .clk(clk), .Q(reg_y_q), .clr(or_1_out));
  Multiplexer #(.select(2), .width(16)) multiplexer_1 (
    .in0(ctrl_q), .in1(reg_x_q), .in2(reg_y_q), .in3({16{1'b0}}), .out(dout), .sel(addr[1:0]));

  // Notes on the sheet:
  //   din: pull=down
endmodule
