// Logisim project Speaker.circ as structural Verilog: 1 circuit, main circuit main
module main (
  input  [6:0] Note,
  input  [6:0] in_2
);

  wire button_1_out;

  Button button_1 (.out(button_1_out));
  // Speaker speaker_1: pin names not known; wires that end beside it: button_1_out, Note, in_2

  // Notes on the sheet:
  //   Reset
  //   Velocity (in midi it means how hard you pressed a note)
endmodule
