// Logisim project MiMo_OR_evo.circ as structural Verilog: 11 circuits, main circuit MiMo_OR_evo
module MiMo_OR_evo (
  input  in_1,
  input  in_2,
  input  in_3,
  input  [15:0] in_4
);

  wire and_1_out, and_2_out, bit_extender_4_out, button_2_out, c, clk, clock_1_out, e_dev0, e_dev1, e_dev2,
       e_ram, gpio_1_p0o, gpio_1_p1o, gpio_1_p2o, gpio_1_p3o, gpio_1_p4o, gpio_1_p5o, gpio_1_p6o, gpio_1_p7o,
       multiplexer_3_out, n, ncmd, or_1_out, reset, twrite, z;
  wire [1:0] addrsel, cond;
  wire [2:0] dsel, ssel, tsel;
  wire [3:0] aluop, bit_extender_3_out, gpio_1_p8o, gpio_1_p12o, icycles;
  wire [6:0] bit_extender_2_out, opcode;
  wire [7:0] adder_1_out, bit_extender_1_out, multiplexer_4_out, multiplexer_5_out, ucounter;
  wire [15:0] address, aluout, cmds, cycles, data, dreg, DROM, framebuffer_1_row0, framebuffer_1_row1,
       framebuffer_1_row2, framebuffer_1_row3, framebuffer_1_row4, framebuffer_1_row5, framebuffer_1_row6,
       framebuffer_1_row7, framebuffer_1_row8, framebuffer_1_row9, framebuffer_1_row10, framebuffer_1_row11,
       framebuffer_1_row12, framebuffer_1_row13, framebuffer_1_row14, framebuffer_1_row15, imreg, irreg,
       multiplexer_2_out, multiplexer_6_out, multiplexer_7_out, pcreg, sreg, treg;
  wire [31:4] CROM;

  // Probe on address
  ROM #(.dataWidth(32)) rom_1 (.addr(ucounter), .data({CROM[31:19], cond, CROM[16:9], addrsel, CROM[6:4], aluop}));
  PC pc_1 (
    .pcreg(pcreg), .imreg(imreg), .sreg(sreg), .pcsel(CROM[10:9]), .pcload(CROM[11]), .clock(clk),
    .reset(reset));
  // Probe on addrsel
  Multiplexer #(.select(2), .width(16)) multiplexer_1 (
    .in0(pcreg), .in1(imreg), .in2(aluout), .in3(sreg), .out(address), .sel(addrsel));
  and and_1 (and_1_out, CROM[6], e_ram);
  and and_2 (and_2_out, ~CROM[6], e_ram);  // AND_Gate
  AddrDecoder addrdecoder_1 (.ram(e_ram), .dev0(e_dev0), .dev1(e_dev1), .dev2(e_dev2), .address(address));
  // Probe on {CROM[31:19], cond, CROM[16:9], addrsel, CROM[6:4], aluop}
  RAM #(.addrWidth(14), .dataWidth(16), .databus("bidir"), .enables("line")) ram_1 (
    .addr(address[13:0]), .we(and_1_out), .oe(and_2_out), .clk(clk), .data(data));
  Button button_1 (.out(reset));
  Clock clock_1 (.out(clock_1_out));
  Button button_2 (.out(button_2_out));
  // Probe on ucounter
  // Probe on aluop
  // Probe on CROM[5:4]
  // Probe on CROM[6]
  // Probe on addrsel
  // Probe on CROM[10:9]
  // Probe on CROM[11]
  // Probe on CROM[12]
  // Probe on CROM[13]
  // Probe on CROM[14]
  // Probe on CROM[16:15]
  // Probe on cond
  // Probe on CROM[19]
  // Probe on CROM[21:20]
  // Probe on CROM[22]
  ROM #(.dataWidth(16)) rom_2 (.addr(ucounter), .data(DROM));
  Register u_ucounter (.D(adder_1_out), .en(1'b1), .clk(clk), .Q(ucounter), .clr(reset));
  // Probe on data
  nor nor_1 (ncmd, ucounter[7], ucounter[6], ucounter[5], ucounter[4], ucounter[2], ucounter[1], ucounter[0], ucounter[3]);
  SuspendHelper suspendhelper_1 (
    .clock_out(clk), .reset(reset), .\continue (button_2_out), .clock(clock_1_out), .pcreg(pcreg),
    .break_addr(in_4), .break_on_addr(in_3), .ucounter(ucounter), .break_on_instr(in_2), .break_on_cycle(in_1));
  Register #(.width(16)) imm (.D(data), .en(CROM[14]), .clk(clk), .Q(imreg), .clr(reset));
  // Probe on CROM[21:20]
  // Probe on DROM
  // Probe on opcode
  assign data = CROM[6] ? multiplexer_2_out : 16'bz;  // Controlled_Buffer controlled_buffer_1
  Multiplexer #(.select(2), .width(16)) multiplexer_2 (
    .in0(pcreg), .in1(dreg), .in2(treg), .in3(aluout), .out(multiplexer_2_out), .sel(CROM[21:20]));
  // Probe on DROM[7:0]
  // Probe on DROM[15:8]
  Multiplexer #(.select(2)) multiplexer_3 (
    .in0(c), .in1(or_1_out), .in2(z), .in3(n), .out(multiplexer_3_out), .sel(cond));
  // Probe on cond
  or or_1 (or_1_out, c, z);
  assign bit_extender_1_out = {{1{1'b0}}, opcode};  // Bit_Extender bit_extender_1
  // Probe on imreg
  Multiplexer #(.width(8)) multiplexer_4 (
    .in0(DROM[7:0]), .in1(DROM[15:8]), .out(multiplexer_4_out), .sel(multiplexer_3_out));
  Multiplexer #(.width(8)) multiplexer_5 (
    .in0({8{1'b0}}), .in1(bit_extender_1_out), .out(multiplexer_5_out), .sel(CROM[19]));
  Bit_Extender #(.in_width(16), .out_width(7), .\type ("zero")) bit_extender_2 (.in(data), .out(bit_extender_2_out));
  CycleCounter cyclecounter_1 (
    .icycles(icycles), .cmds(cmds), .cycles(cycles), .new_ucounter(adder_1_out), .reset(reset), .clock(clk));
  // Probe on opcode
  // Probe on adder_1_out
  Adder adder_1 (.a(multiplexer_4_out), .b(multiplexer_5_out), .out(adder_1_out));  // open: cin, cout
  TTY #(.cols(16), .rows(4)) tty_1 (.data(bit_extender_2_out), .clk(clk), .we(e_dev1), .clr(reset));
  // Probe on tsel
  // Probe on ssel
  // Probe on irreg
  // Probe on dsel
  Multiplexer #(.select(2), .width(16)) multiplexer_6 (
    .in0(data), .in1(imreg), .in2(aluout), .in3(sreg), .out(multiplexer_6_out), .sel(CROM[16:15]));
  // Probe on CROM[16:15]
  IR ir_1 (
    .irreg(irreg), .opcode(opcode), .tsel(tsel), .ssel(ssel), .dsel(dsel), .instruction(data),
    .irload(CROM[13]), .clock(clk), .reset(reset));
  // Probe on CROM[21:20]
  LED led_1 (.in(CROM[22]));
  Bit_Extender #(.in_width(16), .out_width(4), .\type ("zero")) bit_extender_3 (.in(address), .out(bit_extender_3_out));
  // Probe on address
  // Probe on ucounter
  LED led_2 (.in(CROM[19]));
  Bit_Extender #(.in_width(16), .out_width(1), .\type ("zero")) bit_extender_4 (.in(address), .out(bit_extender_4_out));
  // Probe on data
  Multiplexer #(.select(2), .width(16)) multiplexer_7 (
    .in0(treg), .in1(imreg), .in2({16{1'b0}}), .in3(16'h1), .out(multiplexer_7_out), .sel(CROM[5:4]));
  // Probe on CROM[5:4]
  // Probe on {CROM[31:19], cond, CROM[16:9], addrsel, CROM[6:4], aluop}
  // Probe on DROM
  // Probe on cond
  // Probe on CROM[16:15]
  DotMatrix #(.inputtype("row"), .matrixcols(16), .matrixrows(16)) dotmatrix_1 (
    .row0(framebuffer_1_row0), .row1(framebuffer_1_row1), .row2(framebuffer_1_row2),
    .row3(framebuffer_1_row3), .row4(framebuffer_1_row4), .row5(framebuffer_1_row5),
    .row6(framebuffer_1_row6), .row7(framebuffer_1_row7), .row8(framebuffer_1_row8),
    .row9(framebuffer_1_row9), .row10(framebuffer_1_row10), .row11(framebuffer_1_row11),
    .row12(framebuffer_1_row12), .row13(framebuffer_1_row13), .row14(framebuffer_1_row14),
    .row15(framebuffer_1_row15));
  FrameBuffer framebuffer_1 (
    .row0(framebuffer_1_row0), .row4(framebuffer_1_row4), .row8(framebuffer_1_row8),
    .row12(framebuffer_1_row12), .row1(framebuffer_1_row1), .row5(framebuffer_1_row5),
    .row9(framebuffer_1_row9), .row13(framebuffer_1_row13), .row2(framebuffer_1_row2),
    .row6(framebuffer_1_row6), .row10(framebuffer_1_row10), .row14(framebuffer_1_row14),
    .row3(framebuffer_1_row3), .row7(framebuffer_1_row7), .row11(framebuffer_1_row11),
    .row15(framebuffer_1_row15), .data(data), .clk(clk), .reset(reset), .enable(e_dev0),
    .address(bit_extender_3_out));
  // Probe on sreg
  // Probe on multiplexer_7_out
  // Probe on aluop
  LED led_3 (.in(CROM[14]));
  // Probe on pcreg
  // Probe on irreg
  // Probe on imreg
  // Probe on aluout
  LED led_4 (.in(CROM[13]));
  LED led_5 (.in(CROM[12]));
  GPIO gpio_1 (
    .p3o(gpio_1_p3o), .p7o(gpio_1_p7o), .p11o(gpio_1_p8o[3]), .p15o(gpio_1_p12o[3]), .p0o(gpio_1_p0o),
    .p4o(gpio_1_p4o), .p8o(gpio_1_p8o[0]), .p12o(gpio_1_p12o[0]), .p1o(gpio_1_p1o), .p5o(gpio_1_p5o),
    .p9o(gpio_1_p8o[1]), .p13o(gpio_1_p12o[1]), .data_out(data), .p2o(gpio_1_p2o), .p6o(gpio_1_p6o),
    .p10o(gpio_1_p8o[2]), .p14o(gpio_1_p12o[2]), .p3i(gpio_1_p3o), .p7i(gpio_1_p7o), .p11i(gpio_1_p8o[3]),
    .p15i(gpio_1_p12o[3]), .address(bit_extender_4_out), .datawrite(CROM[6]), .reset(reset), .clock(clk),
    .data_in(data), .enable(e_dev2), .p0i(gpio_1_p0o), .p4i(gpio_1_p4o), .p8i(gpio_1_p8o[0]),
    .p12i(gpio_1_p12o[0]), .p1i(gpio_1_p1o), .p5i(gpio_1_p5o), .p9i(gpio_1_p8o[1]), .p13i(gpio_1_p12o[1]),
    .p2i(gpio_1_p2o), .p6i(gpio_1_p6o), .p10i(gpio_1_p8o[2]), .p14i(gpio_1_p12o[2]));  // open: psr
  Registers registers_1 (
    .dreg(dreg), .treg(treg), .sreg(sreg), .clock(clk), .reset(reset), .regval(multiplexer_6_out),
    .tsel(tsel), .ssel(ssel), .dsel(dsel), .twrite(twrite), .swrite(CROM[22]), .dwrite(CROM[12]));  // open: r7, r0, r1, r2, r3, r4, r5, r6
  // Probe on icycles
  // Probe on cycles
  // Probe on cmds
  // Probe on CROM[10:9]
  LED led_6 (.in(CROM[11]));
  // DipSwitch #(.number(4)) dipswitch_1: pin names not known; wires that end beside it: gpio_1_p0o, gpio_1_p1o, gpio_1_p2o, gpio_1_p3o, gpio_1_p4o, gpio_1_p5o
  // DipSwitch #(.number(4)) dipswitch_2: pin names not known; wires that end beside it: gpio_1_p6o, gpio_1_p7o
  Hex_Digit_Display #(.decimalPoint("false")) hex_digit_display_1 (.value(gpio_1_p12o));
  Hex_Digit_Display #(.decimalPoint("false")) hex_digit_display_2 (.value(gpio_1_p8o));
  // Probe on dreg
  ALU alu_1 (.result(aluout), .C(c), .Z(z), .N(n), .B(multiplexer_7_out), .aluop(aluop), .A(sreg));
  // Probe on aluout
  // Probe on addrsel
  // Probe on treg
  LED led_7 (.in(CROM[6]));
  LED led_8 (.in(ncmd));
  // Probe on CROM[5:4]
  // Probe on aluop

  // Other names for the same wires on the sheet: CROM (some bits) = {cond, addrsel, aluop}; op2sel[1:0] = CROM[5:4];
  //   datawrite = CROM[6]; pcsel[1:0] = CROM[10:9]; pcload = CROM[11]; dwrite = CROM[12]; irload = CROM[13];
  //   imload = CROM[14]; regsrc[1:0] = CROM[16:15]; indexsel = CROM[19]; datasel[1:0] = CROM[21:20];
  //   swrite = CROM[22]

  // Notes on the sheet:
  //   contents of rom_1 (hex, n*v repeats v):
  //   2000 80800 11000 11001 11002 11003 11004 11005 11006 11007 11008 11009 1100a 1100b 1100c 1100d 1100e
  //   1100f 30*4000 13*0 4800 4141b0 410030 410031 1000 4*4000 510171 1180 19000 410025 41000a 1100 100140
  //   53*0 11010 11011 11012 11013 11014 11015 11016 11017 11018 11019 1101b 1101c 1101d 1101e 1101f 11000
  //   11001 40001 40001 40001 1 20001 1 40001 1 40021 40021 40021 60021 40021 60021 60021 60021 410171
  //   1080 1000c0 1110 100150 410030 410030 800 a00
  //   Control ROM
  //   Microcode Control Unit
  //   RAM
  //   contents of rom_2 (hex, n*v repeats v):
  //   101 202 16*0 8282 8383 8484 8585 8686 8787 8888 8989 8a8a 8b8b 8c8c 8d8d 8e8e 8f8f 9090 9191 9292
  //   9393 9494 9595 9797 9898 9999 9b9b 9c9c 9d9d 9f9f a1a1 a2a2 abab 13*0 a3a3 abab 0 0 aaaa a4a4 a5a5
  //   a6a6 a7a7 0 a8a8 0 0 a9a9 55*0 15*aaaa abaa abaa abaa aaab aa96 aaab abaa abaa ab9a aaab abaa aaab
  //   aa9e aaab aba0 abaa abaa aaab abab 4*aaaa
  //   Decision ROM
  //   Circuit that helps with debugging.
  //   Can stop the clock on:
  //   - each cycle
  //   - each instuction
  //   - PC = break_addr
  //   'continue' resumes the clock.
  //   Imm. Reg
  //   Based on https://minnie.tuhs.org/Programs/UcodeCPU/
  //   Instruction:
  //   TTY
  //   pc, Rd,
  //   Rt, aluout
  //   Addr, Data bus:
  //   MiMo - Microprogrammed CPU Model
  //   c, c | z,
  //   databus, immed,
  //   z, n
  //   aluout, Rs
  //   Frame Buffer LED 16x16
  //   Current μAddr
  //   Current μInstruction
  //   Next μAddrs
  //   GPIO
  //   Special Registers:
  //   Current μInstruction
  //   pc+1, immed,
  //   pc+immed, Rs
  //   pc, immed,
  //   aluout, Rs
  //   Instruction Cycles
  //   Total Cycles
  //   Total Instructions
  //   Rt, immed,
  //   0, 1
  //   New Instruction
  //   +, -, *, /,
  //   %, &, |, ^,
  //   !&, !|, !, LSL,
  //   LSR, ASR, ROL, ROR
endmodule

module IR (
  input  [15:0] instruction,
  input  irload,
  input  clock,
  input  reset,
  output [15:0] irreg,
  output [6:0] opcode,
  output [2:0] tsel,
  output [2:0] ssel,
  output [2:0] dsel
);

  Register #(.width(16)) register_1 (.D(instruction), .en(irload), .clk(clock), .Q({irreg[15:3], dsel}), .clr(reset));

  assign irreg[2:0] = dsel;
  assign opcode = irreg[15:9];
  assign ssel = irreg[5:3];
  assign tsel = irreg[8:6];

  // Notes on the sheet:
  //   IR Logic
endmodule

module Registers (
  input  twrite,
  input  swrite,
  input  dwrite,
  input  [15:0] regval,
  input  [2:0] tsel,
  input  [2:0] ssel,
  input  [2:0] dsel,
  input  clock,
  input  reset,
  output [15:0] r0,
  output [15:0] r1,
  output [15:0] r2,
  output [15:0] r3,
  output [15:0] r4,
  output [15:0] r5,
  output [15:0] r6,
  output [15:0] r7,
  output [15:0] treg,
  output [15:0] sreg,
  output [15:0] dreg
);

  wire decoder_1_out0, decoder_1_out1, decoder_1_out2, decoder_1_out3, decoder_1_out4, decoder_1_out5,
       decoder_1_out6, decoder_1_out7, decoder_4_out0, decoder_4_out1, decoder_4_out2, decoder_4_out3,
       decoder_4_out4, decoder_4_out5, decoder_4_out6, decoder_4_out7, decoder_5_out0, decoder_5_out1,
       decoder_5_out2, decoder_5_out3, decoder_5_out4, decoder_5_out5, decoder_5_out6, decoder_5_out7,
       decoder_6_out0, decoder_6_out1, decoder_6_out2, decoder_6_out3, decoder_6_out4, decoder_6_out5,
       decoder_6_out6, decoder_6_out7;

  Decoder #(.disabled("Z"), .select(3), .tristate("true")) decoder_1 (
    .out0(decoder_1_out0), .out1(decoder_1_out1), .out2(decoder_1_out2), .out3(decoder_1_out3),
    .out4(decoder_1_out4), .out5(decoder_1_out5), .out6(decoder_1_out6), .out7(decoder_1_out7), .sel(tsel),
    .en(twrite));
  Pull_Resistor pull_resistor_1 (.node(decoder_1_out0));
  Pull_Resistor pull_resistor_2 (.node(decoder_1_out1));
  Pull_Resistor pull_resistor_3 (.node(decoder_1_out2));
  Pull_Resistor pull_resistor_4 (.node(decoder_1_out3));
  Pull_Resistor pull_resistor_5 (.node(decoder_1_out4));
  Pull_Resistor pull_resistor_6 (.node(decoder_1_out5));
  Pull_Resistor pull_resistor_7 (.node(decoder_1_out6));
  Pull_Resistor pull_resistor_8 (.node(decoder_1_out7));
  Decoder #(.disabled("Z"), .select(3), .tristate("true")) decoder_2 (
    .out0(decoder_1_out0), .out1(decoder_1_out1), .out2(decoder_1_out2), .out3(decoder_1_out3),
    .out4(decoder_1_out4), .out5(decoder_1_out5), .out6(decoder_1_out6), .out7(decoder_1_out7), .sel(ssel),
    .en(swrite));
  Decoder #(.disabled("Z"), .select(3), .tristate("true")) decoder_3 (
    .out0(decoder_1_out0), .out1(decoder_1_out1), .out2(decoder_1_out2), .out3(decoder_1_out3),
    .out4(decoder_1_out4), .out5(decoder_1_out5), .out6(decoder_1_out6), .out7(decoder_1_out7), .sel(dsel),
    .en(dwrite));
  Register #(.width(16)) reg0 (.D(regval), .en(decoder_1_out0), .clk(clock), .Q(r0), .clr(reset));
  Register #(.width(16)) reg1 (.D(regval), .en(decoder_1_out1), .clk(clock), .Q(r1), .clr(reset));
  Register #(.width(16)) reg2 (.D(regval), .en(decoder_1_out2), .clk(clock), .Q(r2), .clr(reset));
  Register #(.width(16)) reg3 (.D(regval), .en(decoder_1_out3), .clk(clock), .Q(r3), .clr(reset));
  Register #(.width(16)) reg4 (.D(regval), .en(decoder_1_out4), .clk(clock), .Q(r4), .clr(reset));
  Register #(.width(16)) reg5 (.D(regval), .en(decoder_1_out5), .clk(clock), .Q(r5), .clr(reset));
  Register #(.width(16)) reg6 (.D(regval), .en(decoder_1_out6), .clk(clock), .Q(r6), .clr(reset));
  Register #(.width(16)) reg7 (.D(regval), .en(decoder_1_out7), .clk(clock), .Q(r7), .clr(reset));
  Multiplexer #(.select(3), .width(16)) multiplexer_1 (
    .in0(r0), .in1(r1), .in2(r2), .in3(r3), .in4(r4), .in5(r5), .in6(r6), .in7(r7), .out(treg), .sel(tsel));
  Multiplexer #(.select(3), .width(16)) multiplexer_2 (
    .in0(r0), .in1(r1), .in2(r2), .in3(r3), .in4(r4), .in5(r5), .in6(r6), .in7(r7), .out(sreg), .sel(ssel));
  Multiplexer #(.select(3), .width(16)) multiplexer_3 (
    .in0(r0), .in1(r1), .in2(r2), .in3(r3), .in4(r4), .in5(r5), .in6(r6), .in7(r7), .out(dreg), .sel(dsel));
  Decoder #(.enable("false"), .select(3)) decoder_4 (
    .out0(decoder_4_out0), .out1(decoder_4_out1), .out2(decoder_4_out2), .out3(decoder_4_out3),
    .out4(decoder_4_out4), .out5(decoder_4_out5), .out6(decoder_4_out6), .out7(decoder_4_out7), .sel(tsel));
  LED r0_t (.in(decoder_4_out0));
  LED r1_t (.in(decoder_4_out1));
  LED r2_t (.in(decoder_4_out2));
  LED r3_t (.in(decoder_4_out3));
  LED r4_t (.in(decoder_4_out4));
  LED r5_t (.in(decoder_4_out5));
  LED r6_t (.in(decoder_4_out6));
  Decoder #(.enable("false"), .select(3)) decoder_5 (
    .out0(decoder_5_out0), .out1(decoder_5_out1), .out2(decoder_5_out2), .out3(decoder_5_out3),
    .out4(decoder_5_out4), .out5(decoder_5_out5), .out6(decoder_5_out6), .out7(decoder_5_out7), .sel(ssel));
  LED r0_s (.in(decoder_5_out0));
  LED r1_s (.in(decoder_5_out1));
  LED r7_t (.in(decoder_4_out7));
  LED r2_s (.in(decoder_5_out2));
  LED r3_s (.in(decoder_5_out3));
  LED r4_s (.in(decoder_5_out4));
  LED r5_s (.in(decoder_5_out5));
  LED r6_s (.in(decoder_5_out6));
  LED r7_s (.in(decoder_5_out7));
  Decoder #(.enable("false"), .select(3)) decoder_6 (
    .out0(decoder_6_out0), .out1(decoder_6_out1), .out2(decoder_6_out2), .out3(decoder_6_out3),
    .out4(decoder_6_out4), .out5(decoder_6_out5), .out6(decoder_6_out6), .out7(decoder_6_out7), .sel(dsel));
  LED r0_d (.in(decoder_6_out0));
  LED r1_d (.in(decoder_6_out1));
  LED r2_d (.in(decoder_6_out2));
  LED r3_d (.in(decoder_6_out3));
  LED r4_d (.in(decoder_6_out4));
  LED r5_d (.in(decoder_6_out5));
  LED r6_d (.in(decoder_6_out6));
  LED r7_d (.in(decoder_6_out7));

  // Notes on the sheet:
  //   twrite: pull=down
  //   swrite: pull=down
  //   dwrite: pull=down
  //   Register File
endmodule

module ALU (
  input  [15:0] A,
  input  [15:0] B,
  input  [3:0] aluop,
  output C,
  output Z,
  output N,
  output [15:0] result
);

  wire adder_1_cout, subtractor_1_bout;
  wire [15:0] adder_1_out, and_1_out, divider_1_out, divider_1_rem, multiplier_1_out, nand_1_out, nor_1_out,
       not_1_out, or_1_out, shifter_1_out, shifter_2_out, shifter_3_out, shifter_4_out, shifter_5_out,
       subtractor_1_out, xor_1_out;

  Adder #(.width(16)) adder_1 (.a(A), .b(B), .out(adder_1_out), .cout(adder_1_cout));  // open: cin
  Subtractor #(.width(16)) subtractor_1 (.a(A), .b(B), .out(subtractor_1_out), .bin(1'b0), .bout(subtractor_1_bout));
  Multiplier #(.width(16)) multiplier_1 (.a(A), .b(B), .out(multiplier_1_out), .cin({16{1'b0}}));  // open: cout
  Divider #(.width(16)) divider_1 (.a(A), .b(B), .out(divider_1_out), .rem(divider_1_rem));  // open: upper
  assign not_1_out = ~A;  // NOT_Gate not_1, 16 bits wide
  Shifter #(.width(16)) shifter_1 (.in(A), .\dist (B[3:0]), .out(shifter_1_out));
  Shifter #(.shift("lr"), .width(16)) shifter_2 (.in(A), .\dist (B[3:0]), .out(shifter_2_out));
  Shifter #(.shift("ar"), .width(16)) shifter_3 (.in(A), .\dist (B[3:0]), .out(shifter_3_out));
  Shifter #(.shift("rl"), .width(16)) shifter_4 (.in(A), .\dist (B[3:0]), .out(shifter_4_out));
  Shifter #(.shift("rr"), .width(16)) shifter_5 (.in(A), .\dist (B[3:0]), .out(shifter_5_out));
  assign and_1_out = A & B;  // AND_Gate and_1, 16 bits wide
  assign or_1_out = A | B;  // OR_Gate or_1, 16 bits wide
  assign xor_1_out = A ^ B;  // XOR_Gate xor_1, 16 bits wide
  assign nand_1_out = ~(A & B);  // NAND_Gate nand_1, 16 bits wide
  assign nor_1_out = ~(A | B);  // NOR_Gate nor_1, 16 bits wide
  Multiplexer #(.select(4), .width(16)) multiplexer_1 (
    .in0(adder_1_out), .in1(subtractor_1_out), .in2(multiplier_1_out), .in3(divider_1_out),
    .in4(divider_1_rem), .in5(and_1_out), .in6(or_1_out), .in7(xor_1_out), .in8(nand_1_out), .in9(nor_1_out),
    .in10(not_1_out), .in11(shifter_1_out), .in12(shifter_2_out), .in13(shifter_3_out), .in14(shifter_4_out),
    .in15(shifter_5_out), .out({N, result[14:0]}), .sel(aluop));
  Multiplexer #(.select(4)) multiplexer_2 (
    .in0(adder_1_cout), .in1(subtractor_1_bout), .in2(1'b0), .in3(1'b0), .in4(1'b0), .in5(1'b0), .in6(1'b0),
    .in7(1'b0), .in8(1'b0), .in9(1'b0), .in10(1'b0), .in11(1'b0), .in12(1'b0), .in13(1'b0), .in14(1'b0),
    .in15(1'b0), .out(C), .sel(aluop));
  LED led_1 (.in(C));
  nor nor_2 (Z, N, result[14], result[13], result[12], result[11], result[10], result[9], result[8], result[6], result[5], result[4], result[3], result[2], result[1], result[0], result[7]);
  LED led_2 (.in(Z));
  LED led_3 (.in(N));

  assign result[15] = N;

  // Notes on the sheet:
  //   16-bit ALU
endmodule

module PC (
  input  [15:0] imreg,
  input  pcload,
  input  [15:0] sreg,
  input  clock,
  input  [1:0] pcsel,
  input  reset,
  output [15:0] pcreg
);

  wire [15:0] adder_1_out, adder_2_out, multiplexer_1_out;

  Adder #(.width(16)) adder_1 (.a(pcreg), .b(16'h1), .out(adder_1_out));  // open: cin, cout
  Adder #(.width(16)) adder_2 (.a(pcreg), .b(imreg), .out(adder_2_out));  // open: cin, cout
  Multiplexer #(.select(2), .width(16)) multiplexer_1 (
    .in0(adder_1_out), .in1(imreg), .in2(adder_2_out), .in3(sreg), .out(multiplexer_1_out), .sel(pcsel));
  Register #(.width(16)) register_1 (.D(multiplexer_1_out), .en(pcload), .clk(clock), .Q(pcreg), .clr(reset));

  // Notes on the sheet:
  //   PC Logic
endmodule

module AddrDecoder (
  input  [15:0] address,
  output ram,
  output dev0,
  output dev1,
  output dev2
);

  Decoder #(.enable("false"), .select(2)) decoder_1 (
    .out0(ram), .out1(dev0), .out2(dev1), .out3(dev2), .sel(address[15:14]));

  // Notes on the sheet:
  //   Address Decoder
endmodule

module FrameBuffer (
  input  [15:0] data,
  input  clk,
  input  reset,
  input  enable,
  input  [3:0] address,
  output [15:0] row0,
  output [15:0] row1,
  output [15:0] row2,
  output [15:0] row3,
  output [15:0] row4,
  output [15:0] row5,
  output [15:0] row6,
  output [15:0] row7,
  output [15:0] row8,
  output [15:0] row9,
  output [15:0] row10,
  output [15:0] row11,
  output [15:0] row12,
  output [15:0] row13,
  output [15:0] row14,
  output [15:0] row15
);

  wire decoder_1_out0, decoder_1_out1, decoder_1_out2, decoder_1_out3, decoder_1_out4, decoder_1_out5,
       decoder_1_out6, decoder_1_out7, decoder_1_out8, decoder_1_out9, decoder_1_out10, decoder_1_out11,
       decoder_1_out12, decoder_1_out13, decoder_1_out14, decoder_1_out15;

  Decoder #(.select(4)) decoder_1 (
    .out0(decoder_1_out0), .out1(decoder_1_out1), .out2(decoder_1_out2), .out3(decoder_1_out3),
    .out4(decoder_1_out4), .out5(decoder_1_out5), .out6(decoder_1_out6), .out7(decoder_1_out7),
    .out8(decoder_1_out8), .out9(decoder_1_out9), .out10(decoder_1_out10), .out11(decoder_1_out11),
    .out12(decoder_1_out12), .out13(decoder_1_out13), .out14(decoder_1_out14), .out15(decoder_1_out15),
    .sel(address), .en(enable));
  Register #(.width(16)) register_1 (.D(data), .en(decoder_1_out0), .clk(clk), .Q(row0), .clr(reset));
  Register #(.width(16)) register_2 (.D(data), .en(decoder_1_out4), .clk(clk), .Q(row4), .clr(reset));
  Register #(.width(16)) register_3 (.D(data), .en(decoder_1_out8), .clk(clk), .Q(row8), .clr(reset));
  Register #(.width(16)) register_4 (.D(data), .en(decoder_1_out12), .clk(clk), .Q(row12), .clr(reset));
  Register #(.width(16)) register_5 (.D(data), .en(decoder_1_out1), .clk(clk), .Q(row1), .clr(reset));
  Register #(.width(16)) register_6 (.D(data), .en(decoder_1_out5), .clk(clk), .Q(row5), .clr(reset));
  Register #(.width(16)) register_7 (.D(data), .en(decoder_1_out9), .clk(clk), .Q(row9), .clr(reset));
  Register #(.width(16)) register_8 (.D(data), .en(decoder_1_out13), .clk(clk), .Q(row13), .clr(reset));
  Register #(.width(16)) register_9 (.D(data), .en(decoder_1_out2), .clk(clk), .Q(row2), .clr(reset));
  Register #(.width(16)) register_10 (.D(data), .en(decoder_1_out6), .clk(clk), .Q(row6), .clr(reset));
  Register #(.width(16)) register_11 (.D(data), .en(decoder_1_out10), .clk(clk), .Q(row10), .clr(reset));
  Register #(.width(16)) register_12 (.D(data), .en(decoder_1_out14), .clk(clk), .Q(row14), .clr(reset));
  Register #(.width(16)) register_13 (.D(data), .en(decoder_1_out3), .clk(clk), .Q(row3), .clr(reset));
  Register #(.width(16)) register_14 (.D(data), .en(decoder_1_out7), .clk(clk), .Q(row7), .clr(reset));
  Register #(.width(16)) register_15 (.D(data), .en(decoder_1_out11), .clk(clk), .Q(row11), .clr(reset));
  Register #(.width(16)) register_16 (.D(data), .en(decoder_1_out15), .clk(clk), .Q(row15), .clr(reset));

  // Notes on the sheet:
  //   16x16 Frame Buffer
endmodule

module CycleCounter (
  input  [7:0] new_ucounter,
  input  reset,
  input  clock,
  output [3:0] icycles,
  output [15:0] cycles,
  output [15:0] cmds
);

  wire nor_1_out;

  nor nor_1 (nor_1_out, new_ucounter[7], new_ucounter[6], new_ucounter[5], new_ucounter[4], new_ucounter[2], new_ucounter[1], new_ucounter[0], new_ucounter[3]);
  Counter #(.max('hf), .width(4)) counter_1 (
    .clr(reset), .load(nor_1_out), .clk(clock), .D(4'b0000), .Q(icycles));  // open: up, count, carry
  Counter #(.max('hffff), .width(16)) counter_2 (
    .clr(reset), .count(nor_1_out), .clk(clock), .Q(cmds));  // open: load, up, D, carry
  Counter #(.max('hffff), .width(16)) counter_3 (
    .clr(reset), .clk(clock), .Q(cycles));  // open: load, up, count, D, carry

  // Notes on the sheet:
  //   Counts the number of clock cycles
  //   since the start of current instruction.
  //   Counts the number of instructions
  //   since the start.
  //   Cycle Counter
  //   Counts the number of clock cycles
  //   since the start.
endmodule

module SuspendHelper (
  input  reset,
  input  \continue ,
  input  clock,
  input  [15:0] pcreg,
  input  [15:0] break_addr,
  input  break_on_addr,
  input  [7:0] ucounter,
  input  break_on_instr,
  input  break_on_cycle,
  output clock_out
);

  wire and_1_out, and_2_out, and_3_out, nor_1_out, nor_2_out, nor_3_out, or_1_out, shift_register_1_p4,
       shift_register_1_p5;
  wire [15:0] xor_1_out;

  // Shift_Register #(.length(2), .trigger("falling")) shift_register_1: pin names not known; wires that end beside it: reset, clock, \continue , shift_register_1_p4, shift_register_1_p5
  assign xor_1_out = pcreg ^ break_addr;  // XOR_Gate xor_1, 16 bits wide
  and and_1 (and_1_out, shift_register_1_p4, ~shift_register_1_p5);  // AND_Gate
  nor nor_1 (nor_1_out, xor_1_out[15], xor_1_out[14], xor_1_out[13], xor_1_out[12], xor_1_out[11], xor_1_out[10], xor_1_out[9], xor_1_out[8], xor_1_out[6], xor_1_out[5], xor_1_out[4], xor_1_out[3], xor_1_out[2], xor_1_out[1], xor_1_out[0], xor_1_out[7]);
  and and_2 (and_2_out, nor_1_out, break_on_addr, nor_2_out);
  nor nor_2 (nor_2_out, ucounter[7], ucounter[6], ucounter[5], ucounter[4], ucounter[2], ucounter[1], ucounter[0], ucounter[3]);
  and and_3 (and_3_out, nor_2_out, break_on_instr);
  nor nor_3 (nor_3_out, and_2_out, and_3_out, break_on_cycle);
  or or_1 (or_1_out, and_1_out, nor_3_out);
  and and_4 (clock_out, clock, or_1_out);

  // Notes on the sheet:
  //   Breaks on PC = break_addr
  //   Breaks on each new instruction
  //   Breaks on each clock pulse
  //   Debug Controller
  //   Makes sure the 'continue' button only
  //   lets through 1 clock pulse, until you let go
  //   and press it again.
  //   PC = break_addr?
endmodule

module GPIOPin (
  input  mode,
  input  enable,
  input  datawrite,
  input  pin_in,
  input  data_in,
  input  clk,
  input  reset,
  output data_out,
  output pin_out
);

  wire and_1_out, and_2_out, controlled_buffer_1_out, d_ff_1_q, multiplexer_1_out;

  and and_1 (and_1_out, enable, datawrite);
  D_Flip_Flop d_ff_1 (.D(controlled_buffer_1_out), .clk(clk), .Q(d_ff_1_q), .reset(reset));  // open: Qn, preset
  assign controlled_buffer_1_out = and_1_out ? data_in : 1'bz;  // Controlled_Buffer controlled_buffer_1
  assign pin_out = mode ? d_ff_1_q : 1'bz;  // Controlled_Buffer controlled_buffer_2
  and and_2 (and_2_out, enable, ~datawrite);  // AND_Gate
  assign data_out = and_2_out ? multiplexer_1_out : 1'bz;  // Controlled_Buffer controlled_buffer_3
  Multiplexer multiplexer_1 (.in0(pin_in), .in1(d_ff_1_q), .out(multiplexer_1_out), .sel(mode));

  // Notes on the sheet:
  //   pin_in: pull=down
  //   GPIO Pin
endmodule

module GPIO (
  input  [15:0] data_in,
  input  enable,
  input  address,
  input  datawrite,
  input  reset,
  input  clock,
  input  p0i,
  input  p1i,
  input  p2i,
  input  p3i,
  input  p4i,
  input  p5i,
  input  p6i,
  input  p7i,
  input  p8i,
  input  p9i,
  input  p10i,
  input  p11i,
  input  p12i,
  input  p13i,
  input  p14i,
  input  p15i,
  output [15:0] psr,
  output [15:0] data_out,
  output p0o,
  output p1o,
  output p2o,
  output p3o,
  output p4o,
  output p5o,
  output p6o,
  output p7o,
  output p8o,
  output p9o,
  output p10o,
  output p11o,
  output p12o,
  output p13o,
  output p14o,
  output p15o
);

  wire and_1_out, and_2_out, and_3_out, and_4_out, and_5_out;
  wire [15:0] controlled_buffer_1_out, controlled_buffer_2_out, multiplexer_1_out;

  and and_1 (and_1_out, enable, address);
  assign controlled_buffer_1_out = and_3_out ? controlled_buffer_2_out : 16'bz;  // Controlled_Buffer controlled_buffer_1
  and and_2 (and_2_out, and_1_out, datawrite);
  assign controlled_buffer_2_out = and_2_out ? data_in : 16'bz;  // Controlled_Buffer controlled_buffer_2
  GPIOPin gpiopin_1 (
    .pin_out(p0o), .data_out(controlled_buffer_2_out[0]), .mode(psr[0]), .enable(and_1_out),
    .datawrite(datawrite), .data_in(controlled_buffer_2_out[0]), .clk(clock), .reset(reset), .pin_in(p0i));
  GPIOPin gpiopin_2 (
    .pin_out(p4o), .data_out(controlled_buffer_2_out[4]), .mode(psr[4]), .enable(and_1_out),
    .datawrite(datawrite), .data_in(controlled_buffer_2_out[4]), .clk(clock), .reset(reset), .pin_in(p4i));
  GPIOPin gpiopin_3 (
    .pin_out(p8o), .data_out(controlled_buffer_2_out[8]), .mode(psr[8]), .enable(and_1_out),
    .datawrite(datawrite), .data_in(controlled_buffer_2_out[8]), .clk(clock), .reset(reset), .pin_in(p8i));
  GPIOPin gpiopin_4 (
    .pin_out(p12o), .data_out(controlled_buffer_2_out[12]), .mode(psr[12]), .enable(and_1_out),
    .datawrite(datawrite), .data_in(controlled_buffer_2_out[12]), .clk(clock), .reset(reset), .pin_in(p12i));
  and and_3 (and_3_out, and_1_out, ~datawrite);  // AND_Gate
  Register #(.width(16)) register_1 (.D(data_in), .en(and_4_out), .clk(clock), .Q(psr), .clr(reset));
  and and_4 (and_4_out, enable, ~address, datawrite);  // AND_Gate
  GPIOPin gpiopin_5 (
    .pin_out(p1o), .data_out(controlled_buffer_2_out[1]), .mode(psr[1]), .enable(and_1_out),
    .datawrite(datawrite), .data_in(controlled_buffer_2_out[1]), .clk(clock), .reset(reset), .pin_in(p1i));
  GPIOPin gpiopin_6 (
    .pin_out(p5o), .data_out(controlled_buffer_2_out[5]), .mode(psr[5]), .enable(and_1_out),
    .datawrite(datawrite), .data_in(controlled_buffer_2_out[5]), .clk(clock), .reset(reset), .pin_in(p5i));
  GPIOPin gpiopin_7 (
    .pin_out(p9o), .data_out(controlled_buffer_2_out[9]), .mode(psr[9]), .enable(and_1_out),
    .datawrite(datawrite), .data_in(controlled_buffer_2_out[9]), .clk(clock), .reset(reset), .pin_in(p9i));
  GPIOPin gpiopin_8 (
    .pin_out(p13o), .data_out(controlled_buffer_2_out[13]), .mode(psr[13]), .enable(and_1_out),
    .datawrite(datawrite), .data_in(controlled_buffer_2_out[13]), .clk(clock), .reset(reset), .pin_in(p13i));
  and and_5 (and_5_out, enable, ~datawrite);  // AND_Gate
  assign data_out = and_5_out ? multiplexer_1_out : 16'bz;  // Controlled_Buffer controlled_buffer_3
  Multiplexer #(.width(16)) multiplexer_1 (
    .in0(psr), .in1(controlled_buffer_1_out), .out(multiplexer_1_out), .sel(address));
  GPIOPin gpiopin_9 (
    .pin_out(p2o), .data_out(controlled_buffer_2_out[2]), .mode(psr[2]), .enable(and_1_out),
    .datawrite(datawrite), .data_in(controlled_buffer_2_out[2]), .clk(clock), .reset(reset), .pin_in(p2i));
  GPIOPin gpiopin_10 (
    .pin_out(p6o), .data_out(controlled_buffer_2_out[6]), .mode(psr[6]), .enable(and_1_out),
    .datawrite(datawrite), .data_in(controlled_buffer_2_out[6]), .clk(clock), .reset(reset), .pin_in(p6i));
  GPIOPin gpiopin_11 (
    .pin_out(p10o), .data_out(controlled_buffer_2_out[10]), .mode(psr[10]), .enable(and_1_out),
    .datawrite(datawrite), .data_in(controlled_buffer_2_out[10]), .clk(clock), .reset(reset), .pin_in(p10i));
  GPIOPin gpiopin_12 (
    .pin_out(p14o), .data_out(controlled_buffer_2_out[14]), .mode(psr[14]), .enable(and_1_out),
    .datawrite(datawrite), .data_in(controlled_buffer_2_out[14]), .clk(clock), .reset(reset), .pin_in(p14i));
  GPIOPin gpiopin_13 (
    .pin_out(p3o), .data_out(controlled_buffer_2_out[3]), .mode(psr[3]), .enable(and_1_out),
    .datawrite(datawrite), .data_in(controlled_buffer_2_out[3]), .clk(clock), .reset(reset), .pin_in(p3i));
  GPIOPin gpiopin_14 (
    .pin_out(p7o), .data_out(controlled_buffer_2_out[7]), .mode(psr[7]), .enable(and_1_out),
    .datawrite(datawrite), .data_in(controlled_buffer_2_out[7]), .clk(clock), .reset(reset), .pin_in(p7i));
  GPIOPin gpiopin_15 (
    .pin_out(p11o), .data_out(controlled_buffer_2_out[11]), .mode(psr[11]), .enable(and_1_out),
    .datawrite(datawrite), .data_in(controlled_buffer_2_out[11]), .clk(clock), .reset(reset), .pin_in(p11i));
  GPIOPin gpiopin_16 (
    .pin_out(p15o), .data_out(controlled_buffer_2_out[15]), .mode(psr[15]), .enable(and_1_out),
    .datawrite(datawrite), .data_in(controlled_buffer_2_out[15]), .clk(clock), .reset(reset), .pin_in(p15i));

  // Notes on the sheet:
  //   I regret my decision to emulate bidirectional pins.
  //   This probably has a bunch of bugs.
  //   GPIO
endmodule
