// Logisim project mimo_v04b_DataBus_Demo.circ as structural Verilog: 8 circuits, main circuit MiMo_v04b_OR
// address
module MiMo_v04b_OR (
  input  [15:0] in_1,
  input  imload,
  input  select,
  input  datawrite,
  input  irload,
  input  [1:0] datasel,
  input  [15:0] in_7,
  input  [1:0] regsrc,
  input  [15:0] in_9,
  input  [15:0] in_10,
  input  [15:0] in_11,
  output [15:0] Registers
);

  wire and_1_out, and_2_out, CLK, not_1_out, reset;
  wire [2:0] dregs, sregs, tregs;
  wire [3:0] showhexa_1_digit, showhexa_1_out_2, showhexa_1_out_4, showhexa_1_out_5, showhexa_2_digit,
       showhexa_2_out_2, showhexa_2_out_4, showhexa_2_out_5;
  wire [6:0] opcode;
  wire [15:0] data, immed, irreg, multiplexer_1_out, sreg;

  Hex_Digit_Display hex_digit_display_1 (.value(showhexa_1_out_2));  // open: dp
  ShowHexa showhexa_1 (
    .Data(in_1), .out_4(showhexa_1_out_4), .out_5(showhexa_1_out_5), .out_2(showhexa_1_out_2),
    .Digit(showhexa_1_digit));
  RAM #(.addrWidth(14), .asyncread("true"), .dataWidth(16), .databus("bidir")) ram_1 (
    .addr(in_1[13:0]), .we(and_2_out), .oe(and_1_out), .clk(CLK));  // open: data
  and and_1 (and_1_out, select, not_1_out);
  and and_2 (and_2_out, select, datawrite);
  Hex_Digit_Display hex_digit_display_2 (.value(showhexa_1_out_4));  // open: dp
  Hex_Digit_Display hex_digit_display_3 (.value(showhexa_1_digit));  // open: dp
  not not_1 (not_1_out, datawrite);
  // Probe on datasel
  // Probe on regsrc
  Hex_Digit_Display hex_digit_display_4 (.value(showhexa_1_out_5));  // open: dp
  // Probe on in_1
  // Probe on in_1
  Hex_Digit_Display hex_digit_display_5 (.value(showhexa_2_out_2));  // open: dp
  Hex_Digit_Display hex_digit_display_6 (.value(showhexa_2_digit));  // open: dp
  ShowHexa showhexa_2 (
    .Data(data), .out_4(showhexa_2_out_4), .out_5(showhexa_2_out_5), .out_2(showhexa_2_out_2),
    .Digit(showhexa_2_digit));
  assign data = datawrite ? multiplexer_1_out : 16'bz;  // Controlled_Buffer controlled_buffer_1
  Multiplexer #(.select(2), .width(16)) multiplexer_1 (
    .in0(in_9), .in1(in_10), .in2(in_11), .in3(in_7), .out(multiplexer_1_out), .sel(datasel));
  // Probe on datasel
  Hex_Digit_Display hex_digit_display_7 (.value(showhexa_2_out_4));  // open: dp
  // Probe on in_7
  Hex_Digit_Display hex_digit_display_8 (.value(showhexa_2_out_5));  // open: dp
  // Probe on data
  Instruction_Register_8503bfcc instruction_register_8503bfcc_1 (
    .reset(reset), .irload(irload), .instruction(data), .clock(CLK), .dregsel(dregs), .sregsel(sregs),
    .tregsel(tregs), .opcode(opcode), .Instruction_register_6880d84a(irreg));
  // Probe on irreg
  // Probe on opcode
  Register #(.width(16)) register_1 (.D(data), .en(imload), .Q(immed), .clk(CLK));  // open: clr
  // Probe on immed
  // Probe on Registers
  Multiplexer #(.select(2), .width(16)) multiplexer_2 (
    .in0(data), .in1(immed), .in2(in_7), .in3(sreg), .out(Registers), .sel(regsrc));
  // Probe on regsrc
  Clock clock_1 (.out(CLK));
  // Probe on sregs
  // Probe on dregs
  // Probe on tregs
  Button u_Reset (.out(reset));

  // Other names for the same wires on the sheet: address[15:0] = in_1; aluout[15:0] = in_7; dreg[15:0] = in_10;
  //   pc[15:0] = in_9; RAMSel = select; treg[15:0] = in_11

  // Notes on the sheet:
  //   Address BUS
  //   RAM
  //   datasel : 0..PC 1..Dreg 2..Treg 3..ALE
  //   regsrc:0..DBus 1..IMM 2..ALU 3..Sreg
  //   MiMo - Microprogrammed CPU Model
  //   Data BUS
  //   Address
  //   v0.5
  //   Imm. Reg.
  //   Ins.Reg.
  //   OR
  //   aluout
  //   pc
  //   Dreg
  //   Treg
endmodule

module Instruction_Register_8503bfcc (
  input  [15:0] instruction,
  input  reset,
  input  clock,
  input  irload,
  output [2:0] dregsel,
  output [2:0] sregsel,
  output [2:0] tregsel,
  output [6:0] opcode,
  output [15:0] Instruction_register_6880d84a
);

  Register #(.width(16)) IR (
    .D(instruction), .en(irload), .Q({Instruction_register_6880d84a[15:3], dregsel}), .clk(clock), .clr(reset));

  assign Instruction_register_6880d84a[2:0] = dregsel;
  assign opcode = Instruction_register_6880d84a[15:9];
  assign sregsel = Instruction_register_6880d84a[5:3];
  assign tregsel = Instruction_register_6880d84a[8:6];

  // Notes on the sheet:
  //   IR Logic
endmodule

module Registerfile (
  input  [15:0] regval,
  input  Reset,
  input  clock,
  input  dwrite,
  input  swrite,
  input  twrite,
  input  [2:0] dsel,
  input  [2:0] ssel,
  input  [2:0] tsel,
  output [15:0] r0,
  output [15:0] r1,
  output [15:0] r2,
  output [15:0] r3,
  output [15:0] r4,
  output [15:0] r5,
  output [15:0] r6,
  output [15:0] r7,
  output [15:0] dreg,
  output [15:0] sreg,
  output [15:0] treg
);

  wire demultiplexer_1_out0, demultiplexer_1_out1, demultiplexer_1_out2, demultiplexer_1_out3,
       demultiplexer_1_out4, demultiplexer_1_out5, demultiplexer_1_out6, demultiplexer_1_out7;

  Demultiplexer #(.select(3)) demultiplexer_1 (
    .out0(demultiplexer_1_out0), .out1(demultiplexer_1_out1), .out2(demultiplexer_1_out2),
    .out3(demultiplexer_1_out3), .out4(demultiplexer_1_out4), .out5(demultiplexer_1_out5),
    .out6(demultiplexer_1_out6), .out7(demultiplexer_1_out7), .in(dwrite), .sel(dsel));
  Demultiplexer #(.select(3)) demultiplexer_2 (
    .out0(demultiplexer_1_out0), .out1(demultiplexer_1_out1), .out2(demultiplexer_1_out2),
    .out3(demultiplexer_1_out3), .out4(demultiplexer_1_out4), .out5(demultiplexer_1_out5),
    .out6(demultiplexer_1_out6), .out7(demultiplexer_1_out7), .in(swrite), .sel(ssel));
  Demultiplexer #(.select(3)) demultiplexer_3 (
    .out0(demultiplexer_1_out0), .out1(demultiplexer_1_out1), .out2(demultiplexer_1_out2),
    .out3(demultiplexer_1_out3), .out4(demultiplexer_1_out4), .out5(demultiplexer_1_out5),
    .out6(demultiplexer_1_out6), .out7(demultiplexer_1_out7), .in(twrite), .sel(tsel));
  Register #(.width(16)) register_1 (.D(regval), .en(demultiplexer_1_out0), .Q(r0), .clk(clock), .clr(Reset));
  Register #(.width(16)) register_2 (.D(regval), .en(demultiplexer_1_out1), .Q(r1), .clk(clock), .clr(Reset));
  Register #(.width(16)) register_3 (.D(regval), .en(demultiplexer_1_out2), .Q(r2), .clk(clock), .clr(Reset));
  Register #(.width(16)) register_4 (.D(regval), .en(demultiplexer_1_out3), .Q(r3), .clk(clock), .clr(Reset));
  Register #(.width(16)) register_5 (.D(regval), .en(demultiplexer_1_out4), .Q(r4), .clk(clock), .clr(Reset));
  Register #(.width(16)) register_6 (.D(regval), .en(demultiplexer_1_out5), .Q(r5), .clk(clock), .clr(Reset));
  Register #(.width(16)) register_7 (.D(regval), .en(demultiplexer_1_out6), .Q(r6), .clk(clock), .clr(Reset));
  Register #(.width(16)) register_8 (.D(regval), .en(demultiplexer_1_out7), .Q(r7), .clk(clock), .clr(Reset));
  Multiplexer #(.select(3), .width(16)) multiplexer_1 (
    .in0(r0), .in1(r1), .in2(r2), .in3(r3), .in4(r4), .in5(r5), .in6(r6), .in7(r7), .out(dreg), .sel(dsel));
  Multiplexer #(.select(3), .width(16)) multiplexer_2 (
    .in0(r0), .in1(r1), .in2(r2), .in3(r3), .in4(r4), .in5(r5), .in6(r6), .in7(r7), .out(sreg), .sel(ssel));
  Multiplexer #(.select(3), .width(16)) multiplexer_3 (
    .in0(r0), .in1(r1), .in2(r2), .in3(r3), .in4(r4), .in5(r5), .in6(r6), .in7(r7), .out(treg), .sel(tsel));

  // Notes on the sheet:
  //   Register File
endmodule

module ALU (
  input  [15:0] A,
  input  [15:0] B,
  input  [3:0] aluop,
  output Carry,
  output Zero,
  output Negative,
  output [15:0] Result
);

  wire adder_1_cout, or_2_out, subtractor_1_bout;
  wire [15:0] adder_1_out, and_1_out, divider_1_out, divider_1_rem, multiplier_1_out, nand_1_out, nor_1_out,
       not_1_out, or_1_out, shifter_1_out, shifter_2_out, shifter_3_out, shifter_4_out, shifter_5_out,
       subtractor_1_out, xor_1_out;

  Adder #(.width(16)) adder_1 (.a(A), .b(B), .out(adder_1_out), .cin(1'b0), .cout(adder_1_cout));
  Subtractor #(.width(16)) subtractor_1 (.a(A), .b(B), .out(subtractor_1_out), .bin(1'b0), .bout(subtractor_1_bout));
  Multiplier #(.width(16)) multiplier_1 (.a(A), .b(B), .out(multiplier_1_out), .cin({16{1'b0}}));  // open: cout
  Divider #(.width(16)) divider_1 (.a(A), .b(B), .out(divider_1_out), .upper({16{1'b0}}), .rem(divider_1_rem));
  assign and_1_out = A & B;  // AND_Gate and_1, 16 bits wide
  assign or_1_out = A | B;  // OR_Gate or_1, 16 bits wide
  assign xor_1_out = A ^ B;  // XOR_Gate xor_1, 16 bits wide
  assign nand_1_out = ~(A & B);  // NAND_Gate nand_1, 16 bits wide
  assign nor_1_out = ~(A | B);  // NOR_Gate nor_1, 16 bits wide
  assign not_1_out = ~A;  // NOT_Gate not_1, 16 bits wide
  Shifter #(.width(16)) shifter_1 (.in(A), .\dist (B[3:0]), .out(shifter_1_out));
  Shifter #(.shift("lr"), .width(16)) shifter_2 (.in(A), .\dist (B[3:0]), .out(shifter_2_out));
  Shifter #(.shift("ar"), .width(16)) shifter_3 (.in(A), .\dist (B[3:0]), .out(shifter_3_out));
  Shifter #(.shift("rl"), .width(16)) shifter_4 (.in(A), .\dist (B[3:0]), .out(shifter_4_out));
  Shifter #(.shift("rr"), .width(16)) shifter_5 (.in(A), .\dist (B[3:0]), .out(shifter_5_out));
  Multiplexer #(.select(4), .width(16)) multiplexer_1 (
    .in0(adder_1_out), .in1(subtractor_1_out), .in2(multiplier_1_out), .in3(divider_1_out),
    .in4(divider_1_rem), .in5(and_1_out), .in6(or_1_out), .in7(xor_1_out), .in8(nand_1_out), .in9(nor_1_out),
    .in10(not_1_out), .in11(shifter_1_out), .in12(shifter_2_out), .in13(shifter_3_out), .in14(shifter_4_out),
    .in15(shifter_5_out), .out({Negative, Result[14:0]}), .sel(aluop));
  Multiplexer #(.select(4)) multiplexer_2 (
    .in0(adder_1_cout), .in1(subtractor_1_bout), .in2(1'b0), .in3(1'b0), .in4(1'b0), .in5(1'b0), .in6(1'b0),
    .in7(1'b0), .in8(1'b0), .in9(1'b0), .in10(1'b0), .in11(1'b0), .in12(1'b0), .in13(1'b0), .in14(1'b0),
    .in15(1'b0), .out(Carry), .sel(aluop));
  or or_2 (or_2_out, Result[0], Result[1], Result[2], Result[3], Result[4], Result[5], Result[6], Result[7], Result[9], Result[10], Result[11], Result[12], Result[13], Result[14], Negative, Result[8]);
  not not_2 (Zero, or_2_out);

  assign Result[15] = Negative;

  // Notes on the sheet:
  //   16-bit ALU
endmodule

module PC (
  input  [15:0] imreg,
  input  pcload,
  input  clock,
  input  reset,
  input  [15:0] sreg,
  input  [1:0] pcsel,
  output [15:0] pcout
);

  wire [15:0] adder_1_out, adder_2_out, multiplexer_1_out;

  Adder #(.width(16)) adder_1 (.a(pcout), .b(16'h1), .out(adder_1_out));  // open: cin, cout
  Adder #(.width(16)) adder_2 (.a(pcout), .b(imreg), .out(adder_2_out));  // open: cin, cout
  Multiplexer #(.select(2), .width(16)) multiplexer_1 (
    .in0(adder_1_out), .in1(imreg), .in2(adder_2_out), .in3(sreg), .out(multiplexer_1_out), .sel(pcsel));
  Register #(.width(16)) register_1 (.D(multiplexer_1_out), .en(pcload), .Q(pcout), .clk(clock), .clr(reset));

  // Notes on the sheet:
  //   PC Logic
endmodule

module ShowHexa (
  input  [15:0] Data,
  output [3:0] out_2,
  output [3:0] Digit,
  output [3:0] out_4,
  output [3:0] out_5
);


  assign Digit = Data[11:8];
  assign out_2 = Data[15:12];
  assign out_4 = Data[7:4];
  assign out_5 = Data[3:0];
endmodule

module Frame_Buffer_16x16_e82655da (
  input  [3:0] address,
  input  store,
  input  [15:0] data,
  input  clock,
  input  reset,
  output [15:0] out_6,
  output [15:0] out_7,
  output [15:0] out_8,
  output [15:0] out_9,
  output [15:0] out_10,
  output [15:0] out_11,
  output [15:0] out_12,
  output [15:0] out_13,
  output [15:0] out_14,
  output [15:0] out_15,
  output [15:0] out_16,
  output [15:0] out_17,
  output [15:0] out_18,
  output [15:0] out_19,
  output [15:0] out_20,
  output [15:0] out_21
);

  wire demultiplexer_1_out0, demultiplexer_1_out1, demultiplexer_1_out2, demultiplexer_1_out3,
       demultiplexer_1_out4, demultiplexer_1_out5, demultiplexer_1_out6, demultiplexer_1_out7,
       demultiplexer_1_out8, demultiplexer_1_out9, demultiplexer_1_out10, demultiplexer_1_out11,
       demultiplexer_1_out12, demultiplexer_1_out13, demultiplexer_1_out14, demultiplexer_1_out15;

  Demultiplexer #(.select(4)) demultiplexer_1 (
    .out0(demultiplexer_1_out0), .out1(demultiplexer_1_out1), .out2(demultiplexer_1_out2),
    .out3(demultiplexer_1_out3), .out4(demultiplexer_1_out4), .out5(demultiplexer_1_out5),
    .out6(demultiplexer_1_out6), .out7(demultiplexer_1_out7), .out8(demultiplexer_1_out8),
    .out9(demultiplexer_1_out9), .out10(demultiplexer_1_out10), .out11(demultiplexer_1_out11),
    .out12(demultiplexer_1_out12), .out13(demultiplexer_1_out13), .out14(demultiplexer_1_out14),
    .out15(demultiplexer_1_out15), .in(store), .sel(address));
  Register #(.width(16)) register_1 (.D(data), .en(demultiplexer_1_out0), .Q(out_6), .clk(clock), .clr(reset));
  // Register #(.width(16)) register_2: pin names not known; wires that end beside it: data, demultiplexer_1_out1, data, demultiplexer_1_out2, data, demultiplexer_1_out3, out_7, out_8
  // Register #(.width(16)) register_3: pin names not known; wires that end beside it: data, demultiplexer_1_out2, data, demultiplexer_1_out3, data, demultiplexer_1_out4, out_9
  // Register #(.width(16)) register_4: pin names not known; wires that end beside it: data, demultiplexer_1_out3, data, demultiplexer_1_out4, data, demultiplexer_1_out5, out_10
  // Register #(.width(16)) register_5: pin names not known; wires that end beside it: data, demultiplexer_1_out4, data, demultiplexer_1_out5, data, demultiplexer_1_out6, out_11
  // Register #(.width(16)) register_6: pin names not known; wires that end beside it: data, demultiplexer_1_out5, data, demultiplexer_1_out6, data, demultiplexer_1_out7, out_12
  // Register #(.width(16)) register_7: pin names not known; wires that end beside it: data, demultiplexer_1_out6, data, demultiplexer_1_out7, data, demultiplexer_1_out8, out_13
  // Register #(.width(16)) register_8: pin names not known; wires that end beside it: data, demultiplexer_1_out7, data, demultiplexer_1_out8, data, demultiplexer_1_out9, out_14
  // Register #(.width(16)) register_9: pin names not known; wires that end beside it: data, demultiplexer_1_out8, data, demultiplexer_1_out9, data, demultiplexer_1_out10, out_15
  // Register #(.width(16)) register_10: pin names not known; wires that end beside it: data, demultiplexer_1_out9, data, demultiplexer_1_out10, data, demultiplexer_1_out11, out_16
  // Register #(.width(16)) register_11: pin names not known; wires that end beside it: data, demultiplexer_1_out10, data, demultiplexer_1_out11, data, demultiplexer_1_out12, out_17
  // Register #(.width(16)) register_12: pin names not known; wires that end beside it: data, demultiplexer_1_out11, data, demultiplexer_1_out12, data, demultiplexer_1_out13, out_18
  // Register #(.width(16)) register_13: pin names not known; wires that end beside it: data, demultiplexer_1_out12, data, demultiplexer_1_out13, data, demultiplexer_1_out14, out_19
  // Register #(.width(16)) register_14: pin names not known; wires that end beside it: data, demultiplexer_1_out13, data, demultiplexer_1_out14, data, demultiplexer_1_out15, out_20
  // Register #(.width(16)) register_15: pin names not known; wires that end beside it: data, demultiplexer_1_out14, data, demultiplexer_1_out15, out_21
  // Register #(.width(16)) register_16: pin names not known; wires that end beside it: data, demultiplexer_1_out15
endmodule

module Address_Decoder_25a20b5b (
  input  [15:0] Address,
  output output_0_a756750b,
  output output_1_4eaaf2ee,
  output output_2_962000fe,
  output output_3_4e2177d7
);


  assign output_0_a756750b = 1'b1;
  assign output_1_4eaaf2ee = 1'b1;
  assign output_2_962000fe = 1'b1;
  assign output_3_4e2177d7 = 1'b1;
endmodule
