// Logisim project mimo_v04b_RAM_Demo.circ as structural Verilog: 2 circuits, main circuit MiMo_v04b_OR
// address
module MiMo_v04b_OR (
  input  [15:0] in_1,
  input  select,
  input  datawrite,
  input  [15:0] aluout,
  input  [1:0] datasel,
  input  [15:0] in_6,
  input  [15:0] in_7,
  input  [15:0] in_8
);

  wire and_1_out, and_2_out, CLK, not_1_out, reset;
  wire [3:0] showhexa_1_digit, showhexa_1_out_3, showhexa_1_out_4, showhexa_1_out_5, showhexa_2_digit,
       showhexa_2_out_3, showhexa_2_out_4, showhexa_2_out_5;
  wire [15:0] data, multiplexer_1_out;

  Hex_Digit_Display hex_digit_display_1 (.value(showhexa_1_digit));  // open: dp
  ShowHexa showhexa_1 (
    .Data(in_1), .out_4(showhexa_1_out_4), .out_5(showhexa_1_out_5), .Digit(showhexa_1_digit),
    .out_3(showhexa_1_out_3));
  RAM #(.addrWidth(14), .asyncread("true"), .dataWidth(16), .databus("bidir")) ram_1 (
    .addr(in_1[13:0]), .we(and_2_out), .oe(and_1_out), .clk(CLK));  // open: data
  Hex_Digit_Display hex_digit_display_2 (.value(showhexa_1_out_4));  // open: dp
  Hex_Digit_Display hex_digit_display_3 (.value(showhexa_1_out_3));  // open: dp
  and and_1 (and_1_out, select, not_1_out);
  not not_1 (not_1_out, datawrite);
  and and_2 (and_2_out, select, datawrite);
  Hex_Digit_Display hex_digit_display_4 (.value(showhexa_1_out_5));  // open: dp
  // Probe on in_1
  Hex_Digit_Display hex_digit_display_5 (.value(showhexa_2_digit));  // open: dp
  Hex_Digit_Display hex_digit_display_6 (.value(showhexa_2_out_3));  // open: dp
  ShowHexa showhexa_2 (
    .Data(data), .out_4(showhexa_2_out_4), .out_5(showhexa_2_out_5), .Digit(showhexa_2_digit),
    .out_3(showhexa_2_out_3));
  Hex_Digit_Display hex_digit_display_7 (.value(showhexa_2_out_4));  // open: dp
  Hex_Digit_Display hex_digit_display_8 (.value(showhexa_2_out_5));  // open: dp
  assign data = datawrite ? multiplexer_1_out : 16'bz;  // Controlled_Buffer controlled_buffer_1
  Multiplexer #(.select(2), .width(16)) multiplexer_1 (
    .in0(in_6), .in1(in_7), .in2(in_8), .in3(aluout), .out(multiplexer_1_out), .sel(datasel));
  // Probe on datasel
  // Probe on aluout
  Clock clock_1 (.out(CLK));
  Button u_Reset (.out(reset));

  // Other names for the same wires on the sheet: address[15:0] = in_1; dreg[15:0] = in_7; pc[15:0] = in_6;
  //   RAMSel = select; treg[15:0] = in_8

  // Notes on the sheet:
  //   Address BUS
  //   RAM
  //   MiMo - Microprogrammed CPU Model
  //   Data BUS
  //   v0.5
  //   OR
  //   pc
  //   Dreg
  //   Treg
endmodule

module ShowHexa (
  input  [15:0] Data,
  output [3:0] Digit,
  output [3:0] out_3,
  output [3:0] out_4,
  output [3:0] out_5
);


  assign Digit = Data[15:12];
  assign out_3 = Data[11:8];
  assign out_4 = Data[7:4];
  assign out_5 = Data[3:0];
endmodule
