// Logisim project OR-01_pullup_nor_nand.circ as structural Verilog: 1 circuit, main circuit main
module main (
  input  in_1,
  input  X,
  input  in_3,
  input  Y,
  output out_5,
  output out_6,
  output out_7,
  output out_8
);

  wire transistor_4_out;

  Transistor #(.\type ("n")) transistor_1 (.in(1'b0), .out(out_5), .gate(in_3));
  Pull_Resistor #(.pull(1)) pull_resistor_1 (.node(out_5));
  Transistor #(.\type ("n")) transistor_2 (.in(1'b0), .out(out_5), .gate(in_1));
  nor nor_1 (out_7, in_1, in_3);
  Pull_Resistor #(.pull(1)) pull_resistor_2 (.node(out_6));
  Transistor #(.\type ("n")) transistor_3 (.in(transistor_4_out), .out(out_6), .gate(X));
  Transistor #(.\type ("n")) transistor_4 (.in(1'b0), .out(transistor_4_out), .gate(Y));
  nand nand_1 (out_8, X, Y);

  // Notes on the sheet:
  //   Pull-up NOR
  //   Pull-up NAND
endmodule
