// Logisim project OR-02_pomnilne_celice.circ as structural Verilog: 1 circuit, main circuit main
module main (
  input  S1,
  input  S2,
  input  EN,
  input  R1,
  input  R2,
  input  S,
  input  R,
  output Q1,
  output Q2,
  output not_Q1,
  output not_Q2,
  output Q,
  output not_Q
);

  wire CLK_out, nand_1_out, nand_2_out, nand_5_out, nand_6_out, nand_7_out, nand_8_out, nand_11_out,
       nand_12_out, not_1_out;

  not not_1 (not_1_out, CLK_out);
  Clock CLK (.out(CLK_out));
  nand nand_1 (nand_1_out, S, not_1_out);
  nand nand_2 (nand_2_out, R, not_1_out);
  nand nand_3 (Q1, S1, not_Q1);
  nand nand_4 (not_Q1, Q1, R1);
  LED led_1 (.in(Q1));
  LED led_2 (.in(not_Q1));
  nand nand_5 (nand_5_out, nand_1_out, nand_6_out);
  nand nand_6 (nand_6_out, nand_5_out, nand_2_out);
  nand nand_7 (nand_7_out, CLK_out, nand_5_out);
  nand nand_8 (nand_8_out, nand_6_out, CLK_out);
  nand nand_9 (Q, nand_7_out, not_Q);
  nand nand_10 (not_Q, Q, nand_8_out);
  nand nand_11 (nand_11_out, S2, EN);
  nand nand_12 (nand_12_out, EN, R2);
  LED led_3 (.in(Q));
  LED led_4 (.in(not_Q));
  nand nand_13 (Q2, nand_11_out, not_Q2);
  nand nand_14 (not_Q2, Q2, nand_12_out);
  LED led_5 (.in(Q2));
  LED led_6 (.in(not_Q2));

  // Notes on the sheet:
  //   Aktivno nizko stanje
  //   RS zapah
  //   Input Latch
  //   Sinhronski RS Flip Flop
  //   Output Latch
  //   Sprememba na poz. fronti CLK
  //   RS zapah + Enable
endmodule
