// Logisim project OR-04_Pipelined_vs_nonpipelined.circ as structural Verilog: 3 circuits, main circuit main
module main (
  output [7:0] Non_pipelined_Out,
  output [7:0] Pipelined_Out
);

  wire CLK_out, d_ff_1_q, not_1_out, Reset_out;
  wire [7:0] Address_Counter_q, counter_1_q, rom_1_data, rom_2_data;

  Clock CLK (.out(CLK_out));
  not not_1 (not_1_out, d_ff_1_q);
  D_Flip_Flop d_ff_1 (.D(not_1_out), .clk(CLK_out), .Q(d_ff_1_q));  // open: Qn, preset, reset
  Button Reset (.out(Reset_out));
  ROM rom_1 (.addr(Address_Counter_q), .data(rom_1_data));
  Counter Address_Counter (.Q(Address_Counter_q), .clk(d_ff_1_q), .clr(Reset_out));  // open: load, D, count, carry, up
  ROM rom_2 (.addr(counter_1_q), .data(rom_2_data));
  Counter counter_1 (.Q(counter_1_q), .clk(CLK_out), .clr(Reset_out));  // open: load, D, count, carry, up
  // Probe on rom_1_data
  // Probe on d_ff_1_q
  // Probe on rom_2_data
  // Probe on 8'h1
  Non_pipelined non_pipelined_1 (.In2(8'h1), .In3(rom_1_data), .CLK(d_ff_1_q), .Non_pipelined_Out(Non_pipelined_Out));
  // Probe on 8'h1
  Pipelined pipelined_1 (.In2(8'h1), .In3(rom_2_data), .CLK(CLK_out), .Pipelined_Out(Pipelined_Out));
  // Probe on Non_pipelined_Out
  // Probe on Pipelined_Out

  // Notes on the sheet:
  //   contents of rom_1 (hex, n*v repeats v):
  //   3 2 fc 1 2 fb 1
  //   contents of rom_2 (hex, n*v repeats v):
  //   3 2 fc 1 2 fb 1
  //   Output: [3,5,1,2,4,-1,0,0,...]
  //   Non-Pipelined
  //   Pipelined
endmodule

module Non_pipelined (
  input  [7:0] In2,
  input  [7:0] In3,
  input  CLK,
  output [7:0] Non_pipelined_Out
);

  wire [7:0] adder_1_out, multiplier_1_out;

  Multiplier multiplier_1 (.a(In2), .b(In3), .out(multiplier_1_out));  // open: cin, cout
  Adder adder_1 (.a(multiplier_1_out), .b(Non_pipelined_Out), .out(adder_1_out));  // open: cin, cout
  Register Np_Reg (.D(adder_1_out), .en(1'b1), .clk(CLK), .Q(Non_pipelined_Out));  // open: clr
endmodule

module Pipelined (
  input  [7:0] In2,
  input  [7:0] In3,
  input  CLK,
  output [7:0] Pipelined_Out
);

  wire [7:0] adder_1_out, multiplier_1_out, register_1_q;

  Multiplier multiplier_1 (.a(In2), .b(In3), .out(multiplier_1_out));  // open: cin, cout
  Register register_1 (.D(multiplier_1_out), .en(1'b1), .clk(CLK), .Q(register_1_q));  // open: clr
  Adder adder_1 (.a(register_1_q), .b(Pipelined_Out), .out(adder_1_out));  // open: cin, cout
  Register Np_Reg (.D(adder_1_out), .en(1'b1), .clk(CLK), .Q(Pipelined_Out));  // open: clr
endmodule
